// Logisim project 4BitDispalyer.circ as structural Verilog: 1 circuit, main circuit main
module main (
  input  [3:0] in,
  output out7,
  output out6,
  output out5,
  output out4,
  output out3,
  output out2,
  output out1,
  output out0
);

  Multiplexer #(.select(4), .width(8), .enable("false")) multiplexer_1 (
    .in0(8'hee), .in1(8'h28), .in2(8'hdc), .in3(8'hd6), .in4(8'hb8), .in5(8'h76), .in6(8'h7e), .in7(8'hc2),
    .in8(8'hfe), .in9(8'hf6), .in10({8{1'b0}}), .in11({8{1'b0}}), .in12({8{1'b0}}), .in13({8{1'b0}}),
    .in14({8{1'b0}}), .in15({8{1'b0}}), .out({out7, out6, out5, out4, out3, out2, out1, out0}), .sel(in));
  _7_Segment_Display u_7_segment_display_1 (
    .g(out4), .f(out5), .a(out6), .b(out7), .e(out3), .d(out2), .c(out1), .dp(out0));
endmodule
