// Logisim project ControlUnit.circ as structural Verilog: 1 circuit, main circuit main
module main (
  input  input_eq_word_i,
  input  i_gt_0,
  input  i_eq_0,
  input  i_lt_0,
  input  i_gt_nOc,
  input  i_eq_nOc,
  input  i_lt_nOc,
  input  nOc_eq_f,
  input  mistake_eq_10,
  input  isFound,
  input  scan,
  input  run,
  input  \new ,
  input  CLK,
  output getWord,
  output clear_i,
  output clear_f,
  output clear_mistake,
  output isFound_clear,
  output starToTemp,
  output set_T,
  output count_i,
  output scan_Led,
  output isFound_en,
  output count_f,
  output isFound_2,
  output count_i_2,
  output count_mistake,
  output load_i,
  output clearScreen,
  output printAvailable,
  output ToPrint,
  output countWin,
  output countLost,
  output clear_nOc
);

  wire and_1_out, not_1_out, not_2_out, not_3_out, not_4_out, not_5_out, not_6_out, not_7_out, not_8_out,
       not_9_out, not_10_out, not_11_out, not_12_out, not_13_out, not_14_out, not_15_out, not_16_out,
       not_17_out, not_18_out, not_19_out, not_20_out, not_21_out, not_22_out, not_23_out, not_24_out,
       not_25_out, not_26_out, not_27_out, not_28_out, not_29_out, not_30_out, not_31_out, not_32_out,
       not_33_out, not_34_out, not_35_out, not_36_out, not_37_out, not_38_out, not_39_out, not_40_out,
       not_41_out, not_42_out, not_43_out, not_44_out, not_45_out, not_46_out, not_47_out, not_48_out,
       not_49_out, not_50_out, not_51_out, not_52_out, not_53_out, not_54_out, not_55_out, not_56_out,
       not_57_out, not_58_out, not_59_out, not_60_out, not_61_out, not_62_out, not_63_out, not_64_out,
       not_65_out, not_66_out, not_67_out, not_68_out, not_69_out, not_70_out, not_71_out, not_72_out,
       not_73_out, not_74_out, not_75_out, not_76_out, not_77_out, not_78_out, not_79_out, not_80_out,
       not_81_out, S6_out, S10_out, S13_out, S14_out, S17_out, S21_out, S22_out, S24_out, S25_out;
  wire [4:0] multiplexer_1_out, N0_n0, register_1_q;

  Register #(.width(5)) register_1 (.D(multiplexer_1_out), .en(1'b1), .Q(register_1_q), .clk(CLK));  // open: clr
  No N0 (
    .s0(register_1_q[0]), .s1(register_1_q[1]), .s2(register_1_q[2]), .s3(register_1_q[3]),
    .s4(register_1_q[4]), .run(run), .i_lt_nOc(i_lt_nOc), .i_eq_nOc(i_eq_nOc), .i_gt_nOc(i_gt_nOc),
    .input_eq_word(input_eq_word_i), .isFound(isFound), .mistake_eq_10(mistake_eq_10), .nOc_eq_f(nOc_eq_f),
    .scan(scan), .\new (\new ), .n0(N0_n0[0]));
  N1 N1 (
    .s4(register_1_q[4]), .s3(register_1_q[3]), .s2(register_1_q[2]), .s1(register_1_q[1]),
    .s0(register_1_q[0]), .scan(scan), .i_eq_noc(i_eq_nOc), .i_gt_noc(i_gt_nOc),
    .in_eq_word(input_eq_word_i), .i_lt_0(i_lt_0), .noc_eq_f(nOc_eq_f), .mistake_eq_10(mistake_eq_10),
    .i_lt_noc(i_lt_nOc), .n1(N0_n0[1]));
  N2 N2 (
    .s4(register_1_q[4]), .s3(register_1_q[3]), .s2(register_1_q[2]), .s1(register_1_q[1]),
    .s0(register_1_q[0]), .i_eq_noc(i_eq_nOc), .i_gt_noc(i_gt_nOc), .noc_eq_f(nOc_eq_f),
    .mistake_eq_10(mistake_eq_10), .n2(N0_n0[2]));
  NN3 N3 (
    .s4(register_1_q[4]), .s3(register_1_q[3]), .s2(register_1_q[2]), .s1(register_1_q[1]),
    .s0(register_1_q[0]), .n3(N0_n0[3]));
  N4 N4 (
    .s4(register_1_q[4]), .s3(register_1_q[3]), .s2(register_1_q[2]), .s1(register_1_q[1]),
    .s0(register_1_q[0]), .nOc_eq_f(nOc_eq_f), .mistake_eq_10(mistake_eq_10), .n4(N0_n0[4]));
  not not_1 (not_1_out, register_1_q[3]);
  not not_2 (not_2_out, register_1_q[2]);
  and and_1 (and_1_out, register_1_q[4], not_1_out, not_2_out, register_1_q[1], not_3_out, not_4_out, not_5_out);
  not not_3 (not_3_out, register_1_q[0]);
  not not_4 (not_4_out, mistake_eq_10);
  not not_5 (not_5_out, nOc_eq_f);
  Multiplexer #(.width(5), .enable("false")) multiplexer_1 (
    .in0(N0_n0), .in1(5'b00101), .out(multiplexer_1_out), .sel(and_1_out));
  not not_6 (not_6_out, register_1_q[4]);
  not not_7 (not_7_out, register_1_q[3]);
  not not_8 (not_8_out, register_1_q[2]);
  not not_9 (not_9_out, register_1_q[1]);
  not not_10 (not_10_out, register_1_q[0]);
  not not_11 (not_11_out, register_1_q[4]);
  not not_12 (not_12_out, register_1_q[3]);
  not not_13 (not_13_out, register_1_q[2]);
  not not_14 (not_14_out, register_1_q[1]);
  not not_15 (not_15_out, register_1_q[4]);
  not not_16 (not_16_out, register_1_q[3]);
  not not_17 (not_17_out, register_1_q[2]);
  not not_18 (not_18_out, register_1_q[0]);
  not not_19 (not_19_out, register_1_q[4]);
  not not_20 (not_20_out, register_1_q[3]);
  not not_21 (not_21_out, register_1_q[2]);
  not not_22 (not_22_out, register_1_q[4]);
  not not_23 (not_23_out, register_1_q[3]);
  not not_24 (not_24_out, register_1_q[1]);
  not not_25 (not_25_out, register_1_q[0]);
  not not_26 (not_26_out, register_1_q[4]);
  not not_27 (not_27_out, register_1_q[3]);
  not not_28 (not_28_out, register_1_q[1]);
  not not_29 (not_29_out, register_1_q[4]);
  not not_30 (not_30_out, register_1_q[3]);
  not not_31 (not_31_out, register_1_q[0]);
  not not_32 (not_32_out, register_1_q[4]);
  not not_33 (not_33_out, register_1_q[3]);
  not not_34 (not_34_out, register_1_q[4]);
  not not_35 (not_35_out, register_1_q[2]);
  not not_36 (not_36_out, register_1_q[1]);
  not not_37 (not_37_out, register_1_q[0]);
  not not_38 (not_38_out, register_1_q[4]);
  not not_39 (not_39_out, register_1_q[2]);
  not not_40 (not_40_out, register_1_q[1]);
  not not_41 (not_41_out, register_1_q[4]);
  not not_42 (not_42_out, register_1_q[2]);
  not not_43 (not_43_out, register_1_q[0]);
  not not_44 (not_44_out, register_1_q[4]);
  not not_45 (not_45_out, register_1_q[2]);
  not not_46 (not_46_out, register_1_q[4]);
  not not_47 (not_47_out, register_1_q[1]);
  not not_48 (not_48_out, register_1_q[0]);
  not not_49 (not_49_out, register_1_q[4]);
  not not_50 (not_50_out, register_1_q[1]);
  not not_51 (not_51_out, register_1_q[4]);
  not not_52 (not_52_out, register_1_q[0]);
  not not_53 (not_53_out, register_1_q[4]);
  not not_54 (not_54_out, register_1_q[3]);
  not not_55 (not_55_out, register_1_q[2]);
  not not_56 (not_56_out, register_1_q[1]);
  not not_57 (not_57_out, register_1_q[0]);
  not not_58 (not_58_out, register_1_q[3]);
  not not_59 (not_59_out, register_1_q[2]);
  not not_60 (not_60_out, register_1_q[1]);
  not not_61 (not_61_out, register_1_q[3]);
  not not_62 (not_62_out, register_1_q[2]);
  not not_63 (not_63_out, register_1_q[0]);
  not not_64 (not_64_out, register_1_q[3]);
  not not_65 (not_65_out, register_1_q[2]);
  not not_66 (not_66_out, register_1_q[3]);
  not not_67 (not_67_out, register_1_q[1]);
  not not_68 (not_68_out, register_1_q[0]);
  not not_69 (not_69_out, register_1_q[3]);
  not not_70 (not_70_out, register_1_q[1]);
  not not_71 (not_71_out, register_1_q[3]);
  not not_72 (not_72_out, register_1_q[0]);
  not not_73 (not_73_out, register_1_q[3]);
  not not_74 (not_74_out, register_1_q[2]);
  not not_75 (not_75_out, register_1_q[1]);
  not not_76 (not_76_out, register_1_q[0]);
  not not_77 (not_77_out, register_1_q[2]);
  not not_78 (not_78_out, register_1_q[1]);
  not not_79 (not_79_out, register_1_q[2]);
  not not_80 (not_80_out, register_1_q[0]);
  not not_81 (not_81_out, register_1_q[2]);
  and S0 (getWord, not_6_out, not_7_out, not_8_out, not_9_out, not_10_out);
  and S1 (clear_f, not_11_out, not_12_out, not_13_out, not_14_out, register_1_q[0]);
  // AND_Gate S2 has open pins: in0=not_15_out, in1=not_16_out, in2=not_17_out, in3=register_1_q[1], in4=not_18_out, out=open
  and S3 (starToTemp, not_19_out, not_20_out, not_21_out, register_1_q[1], register_1_q[0]);
  and S4 (count_i, not_22_out, not_23_out, register_1_q[2], not_24_out, not_25_out);
  and S5 (scan_Led, not_26_out, not_27_out, register_1_q[2], not_28_out, register_1_q[0]);
  and S6 (S6_out, not_29_out, not_30_out, register_1_q[2], register_1_q[1], not_31_out);
  // AND_Gate S7 has open pins: in0=not_32_out, in1=not_33_out, in2=register_1_q[2], in3=register_1_q[1], in4=register_1_q[0], out=open
  // AND_Gate S8 has open pins: in0=not_34_out, in1=register_1_q[3], in2=not_35_out, in3=not_36_out, in4=not_37_out, out=open
  and S9 (count_f, not_38_out, register_1_q[3], not_39_out, not_40_out, register_1_q[0]);
  and S10 (S10_out, not_41_out, register_1_q[3], not_42_out, register_1_q[1], not_43_out);
  // AND_Gate S11 has open pins: in0=not_44_out, in1=register_1_q[3], in2=not_45_out, in3=register_1_q[1], in4=register_1_q[0], out=open
  and S12 (count_mistake, not_46_out, register_1_q[3], register_1_q[2], not_47_out, not_48_out);
  and S13 (S13_out, not_49_out, register_1_q[3], register_1_q[2], not_50_out, register_1_q[0]);
  and S14 (S14_out, not_51_out, register_1_q[3], register_1_q[2], register_1_q[1], not_52_out);
  // AND_Gate S15 has open pins: in0=not_53_out, in1=register_1_q[3], in2=register_1_q[2], in3=register_1_q[1], in4=register_1_q[0], out=open
  and S16 (ToPrint, register_1_q[4], not_54_out, not_55_out, not_56_out, not_57_out);
  and S17 (S17_out, register_1_q[4], not_58_out, not_59_out, not_60_out, register_1_q[0]);
  // AND_Gate S18 has open pins: in0=register_1_q[4], in1=not_61_out, in2=not_62_out, in3=register_1_q[1], in4=not_63_out, out=open
  and S19 (countWin, register_1_q[4], not_64_out, not_65_out, register_1_q[1], register_1_q[0]);
  and S20 (countLost, register_1_q[4], not_66_out, register_1_q[2], not_67_out, not_68_out);
  and S21 (S21_out, register_1_q[4], not_69_out, register_1_q[2], not_70_out, register_1_q[0]);
  and S22 (S22_out, register_1_q[4], not_71_out, register_1_q[2], register_1_q[1], not_72_out);
  // AND_Gate S23 has open pins: in0=register_1_q[4], in1=not_73_out, in2=register_1_q[2], in3=register_1_q[1], in4=register_1_q[0], out=open
  and S24 (S24_out, register_1_q[4], register_1_q[3], not_74_out, not_75_out, not_76_out);
  and S25 (S25_out, register_1_q[4], register_1_q[3], not_77_out, not_78_out, register_1_q[0]);
  // AND_Gate S26 has open pins: in0=register_1_q[4], in1=register_1_q[3], in2=not_79_out, in3=register_1_q[1], in4=not_80_out, out=open
  and S27 (clear_nOc, register_1_q[4], register_1_q[3], not_81_out, register_1_q[1], register_1_q[0]);
  or or_1 (clear_i, clear_f, S6_out);
  or or_2 (set_T, starToTemp, count_f);
  or or_3 (isFound_en, S6_out, count_f);
  or or_4 (count_i_2, S10_out, S17_out, S25_out);
  or or_5 (load_i, S13_out, S17_out, S21_out, S25_out);
  or or_6 (clearScreen, S14_out, S22_out, clear_nOc);
  or or_7 (printAvailable, ToPrint, S24_out);

  assign clear_mistake = clear_f;
  assign isFound_2 = count_f;
  assign isFound_clear = clear_f;

  // Notes on the sheet:
  //   s4
  //   s2
  //   s3
  //   s1
  //   s0
endmodule
