// Logisim project DataPath.circ as structural Verilog: 1 circuit, main circuit main
module main (
  input  [6:0] char_W,
  input  shift_W,
  input  getWord,
  input  clear_W,
  input  set_W,
  input  load_i,
  input  count_i,
  input  clear_i,
  input  load_nOc,
  input  [3:0] nOc_in,
  input  load_f,
  input  [3:0] f_in,
  input  count_f,
  input  clear_f,
  input  ToPrint,
  input  StarToTemp,
  input  clear_T,
  input  set_T,
  input  L_mistake,
  input  [3:0] mistake_in,
  input  count_mistake,
  input  clear_mistake,
  input  L_win,
  input  [3:0] win_in,
  input  count_win,
  input  clear_win,
  input  L_lost,
  input  [3:0] lost_in,
  input  count_lost,
  input  clear_lsot,
  input  isFound,
  input  isFound_en,
  input  isFound_clear,
  input  CLK,
  output input_eq_word_i,
  output [7:0] word_i,
  output i_gt_0,
  output i_eq_0,
  output i_lt_0,
  output i_gt_nOc,
  output i_eq_nOc,
  output i_lt_nOc,
  output [3:0] numberOfChar,
  output nOc_gt_f,
  output nOc_eq_f,
  output nOc_lt_f,
  output [7:0] selectedToPrint,
  output [7:0] temp_i,
  output mistake_gt_10,
  output mistake_eq_10,
  output mistake_lt_10,
  output [3:0] mistakes,
  output [3:0] win_out,
  output [3:0] lost_out,
  output isFound_out
);

  wire comparator_1_eq, multiplexer_1_out, multiplexer_2_out, multiplexer_4_out;
  wire [2:0] bit_extender_1_out, bit_extender_3_out;
  wire [3:0] foundLetter_q, i_q, subtractor_1_out;
  wire [4:0] bit_extender_4_out, bit_extender_5_out, bit_extender_6_out, bit_extender_7_out;
  wire [7:0] bit_extender_2_out, input_q, multiplexer_3_out;

  Multiplexer #(.enable("false")) multiplexer_1 (
    .in0(shift_W), .in1(1'b0), .out(multiplexer_1_out), .sel(comparator_1_eq));
  Multiplexer #(.enable("false")) multiplexer_2 (.in0(1'b0), .in1(shift_W), .out(multiplexer_2_out), .sel(getWord));
  Bit_Extender #(.in_width(4), .out_width(3)) bit_extender_1 (.in(i_q), .out(bit_extender_1_out));
  Multiplexer #(.width(8), .enable("false")) multiplexer_3 (
    .in0(input_q), .in1(8'h2a), .out(multiplexer_3_out), .sel(StarToTemp));
  assign bit_extender_2_out = {{1{1'b0}}, char_W};  // Bit_Extender bit_extender_2
  Multiplexer #(.enable("false")) multiplexer_4 (
    .in0(1'b0), .in1(multiplexer_1_out), .out(multiplexer_4_out), .sel(getWord));
  Register \input  (.D(bit_extender_2_out), .en(shift_W), .Q(input_q), .clk(CLK));  // open: clr
  staticArray_main Word (
    .\input (bit_extender_2_out), .shift(multiplexer_2_out), .CLK(CLK), .clear(clear_W),
    .index(bit_extender_1_out), .set(set_W), .out(word_i));
  Counter #(.width(4), .max('hf)) i (
    .load(load_i), .D(subtractor_1_out), .count(count_i), .Q(i_q), .clk(CLK), .clr(clear_i));  // open: carry
  Counter #(.width(4), .max('hf)) u_numberOfChar (
    .load(load_nOc), .D(nOc_in), .count(multiplexer_4_out), .Q(numberOfChar), .clk(CLK), .clr(clear_W));  // open: carry
  Counter #(.width(4), .max('hf)) foundLetter (
    .load(load_f), .D(f_in), .count(count_f), .Q(foundLetter_q), .clk(CLK), .clr(clear_f));  // open: carry
  Bit_Extender #(.in_width(4), .out_width(3)) bit_extender_3 (.in(i_q), .out(bit_extender_3_out));
  staticArray_main temp (
    .\input (multiplexer_3_out), .shift(1'b0), .CLK(CLK), .clear(clear_T), .index(bit_extender_3_out),
    .set(set_T), .out(temp_i));
  Counter #(.width(4), .max('hf)) u_mistakes (
    .load(L_mistake), .D(mistake_in), .count(count_mistake), .Q(mistakes), .clk(CLK), .clr(clear_mistake));  // open: carry
  Counter #(.width(4), .max('hf)) win (
    .load(L_win), .D(win_in), .count(count_win), .Q(win_out), .clk(CLK), .clr(clear_win));  // open: carry
  Counter #(.width(4), .max('hf)) lost (
    .load(L_lost), .D(lost_in), .count(count_lost), .Q(lost_out), .clk(CLK), .clr(clear_lsot));  // open: carry
  Register #(.width(1)) u_isFound (.D(isFound), .en(isFound_en), .Q(isFound_out), .clk(CLK), .clr(isFound_clear));
  assign bit_extender_4_out = {{1{1'b0}}, i_q};  // Bit_Extender bit_extender_4
  Comparator #(.width(4)) comparator_1 (.a(numberOfChar), .b(4'b1000), .eq(comparator_1_eq));  // open: gt, lt
  assign bit_extender_5_out = {{1{1'b0}}, foundLetter_q};  // Bit_Extender bit_extender_5
  assign bit_extender_6_out = {{1{1'b0}}, mistakes};  // Bit_Extender bit_extender_6
  assign bit_extender_7_out = {{1{1'b0}}, numberOfChar};  // Bit_Extender bit_extender_7
  Comparator comparator_2 (.a(input_q), .b(word_i), .eq(input_eq_word_i));  // open: gt, lt
  Comparator #(.width(4)) comparator_3 (.a(i_q), .b(4'b0000), .gt(i_gt_0), .eq(i_eq_0), .lt(i_lt_0));
  Comparator #(.width(5)) comparator_4 (
    .a(bit_extender_4_out), .b(bit_extender_7_out), .gt(i_gt_nOc), .eq(i_eq_nOc), .lt(i_lt_nOc));
  Comparator #(.width(5)) comparator_5 (
    .a(bit_extender_7_out), .b(bit_extender_5_out), .gt(nOc_gt_f), .eq(nOc_eq_f), .lt(nOc_lt_f));
  Comparator #(.width(5)) comparator_6 (
    .a(bit_extender_6_out), .b(5'b01010), .gt(mistake_gt_10), .eq(mistake_eq_10), .lt(mistake_lt_10));
  Subtractor #(.width(4)) subtractor_1 (.a(numberOfChar), .b(4'b0001), .out(subtractor_1_out));  // open: bin, bout
  Multiplexer #(.width(8), .enable("false")) multiplexer_5 (
    .in0(word_i), .in1(temp_i), .out(selectedToPrint), .sel(ToPrint));
endmodule
