// Logisim project Keyboard.circ as structural Verilog: 1 circuit, main circuit main
module main (
  input  CLK,
  input  CAPS_UNLOCK,
  input  Q,
  input  W,
  input  E,
  input  R,
  input  T,
  input  Y,
  input  U,
  input  I,
  input  O,
  input  P,
  input  A,
  input  S,
  input  D,
  input  F,
  input  G,
  input  H,
  input  J,
  input  K,
  input  L,
  input  Z,
  input  X,
  input  C,
  input  V,
  input  B,
  input  N,
  input  M,
  output [6:0] theOutput,
  output outputAvailable
);

  wire or_6_out;
  wire [4:0] or_5_out;
  wire [6:0] multiplexer_1_out;

  or or_1 (or_5_out[4], Q, R, S, T, U, V, W, X, Y, Z);
  or or_2 (or_5_out[3], I, J, K, L, M, N, O, P, Y, Z);
  or or_3 (or_5_out[2], E, F, G, H, M, N, O, P, U, V, W, X);
  or or_4 (or_5_out[1], C, D, G, H, K, L, O, P, S, T, W, X);
  or or_5 (or_5_out[0], B, D, F, H, J, L, N, P, R, T, V, X, Z);
  or or_6 (or_6_out, or_5_out[4], or_5_out[3], or_5_out[2], or_5_out[1], or_5_out[0], A);
  buttonHandler_main main_1 (.Button_in(or_6_out), .CLK(CLK), .Button_out(outputAvailable));
  Multiplexer #(.width(7), .enable("false")) multiplexer_1 (
    .in0(7'b1000001), .in1(7'b1100001), .out(multiplexer_1_out), .sel(CAPS_UNLOCK));
  Adder #(.width(7)) adder_1 (.a({2'b00, or_5_out}), .b(multiplexer_1_out), .out(theOutput));  // open: cin, cout
endmodule
