// Logisim project Main.circ as structural Verilog: 1 circuit, main circuit main
module main (
  input  CAPS_UNLOCK,
  input  [3:0] in_2,
  input  [3:0] in_3,
  input  [3:0] in_4,
  input  [3:0] in_5,
  input  [3:0] in_6
);

  wire clear_Lost_out, clear_Temp_out, clear_Win_out, clear_Word_out, clock_1_out, ControlUnit_clear_f,
       ControlUnit_clear_i, ControlUnit_clear_mistake, ControlUnit_clear_noc, ControlUnit_clearscreen,
       ControlUnit_count_f, ControlUnit_count_i, ControlUnit_count_mistake, ControlUnit_countlost,
       ControlUnit_countwin, ControlUnit_getword, ControlUnit_isfound_2, ControlUnit_isfound_clear,
       ControlUnit_isfound_en, ControlUnit_load_i, ControlUnit_printavailable, ControlUnit_scan_led,
       ControlUnit_set_t, ControlUnit_startotemp, ControlUnit_toprint, DataPath_i_eq_0, DataPath_i_eq_noc,
       DataPath_i_gt_0, DataPath_i_gt_noc, DataPath_i_lt_0, DataPath_i_lt_noc, DataPath_input_eq_word_i,
       DataPath_isfound_out, DataPath_mistake_eq_10, DataPath_noc_eq_f, main_1_outputavailable, main_2_out0,
       main_2_out1, main_2_out2, main_2_out3, main_2_out4, main_2_out5, main_2_out6, main_2_out7,
       main_3_out0, main_3_out1, main_3_out2, main_3_out3, main_3_out4, main_3_out5, main_3_out6,
       main_3_out7, main_4_out0, main_4_out1, main_4_out2, main_4_out3, main_4_out4, main_4_out5,
       main_4_out6, main_4_out7, main_5__0, main_5__1, main_5__2, main_5__3, main_5__4, main_5__5, main_5__6,
       main_5__7, main_5__8, main_5__9, new_out, run_out;
  wire [3:0] DataPath_lost_out, DataPath_mistakes, DataPath_numberofchar, DataPath_win_out;
  wire [6:0] bit_extender_1_out, main_1_theoutput, Z_out;
  wire [7:0] DataPath_selectedtoprint;
  wire [8:0] L_out;
  wire [9:0] P_out;

  Button clear_Word (.out(clear_Word_out));
  Button clear_Win (.out(clear_Win_out));
  Button clear_Lost (.out(clear_Lost_out));
  Button Q (.out(P_out[9]));
  Button W (.out(P_out[8]));
  Button A (.out(L_out[8]));
  Button Z (.out(Z_out[0]));
  Clock clock_1 (.out(clock_1_out));
  Button R (.out(P_out[6]));
  Button E (.out(P_out[7]));
  Button S (.out(L_out[7]));
  Button D (.out(L_out[6]));
  Button X (.out(Z_out[1]));
  Button C (.out(Z_out[2]));
  Button T (.out(P_out[5]));
  Button Y (.out(P_out[4]));
  Button F (.out(L_out[5]));
  Button G (.out(L_out[4]));
  Button V (.out(Z_out[3]));
  Button B (.out(Z_out[4]));
  Keyboard_main main_1 (
    .Q(P_out[9]), .W(P_out[8]), .E(P_out[7]), .R(P_out[6]), .T(P_out[5]), .Y(P_out[4]), .U(P_out[3]),
    .I(P_out[2]), .O(P_out[1]), .P(P_out[0]), .A(L_out[8]), .S(L_out[7]), .D(L_out[6]), .F(L_out[5]),
    .G(L_out[4]), .H(L_out[3]), .J(L_out[2]), .K(L_out[1]), .L(L_out[0]), .Z(Z_out[0]), .X(Z_out[1]),
    .C(Z_out[2]), .V(Z_out[3]), .B(Z_out[4]), .N(Z_out[5]), .M(Z_out[6]), .CLK(clock_1_out),
    .CAPS_UNLOCK(CAPS_UNLOCK), .theOutput(main_1_theoutput), .outputAvailable(main_1_outputavailable));
  Button U (.out(P_out[3]));
  Button I (.out(P_out[2]));
  Button H (.out(L_out[3]));
  Button J (.out(L_out[2]));
  Button M (.out(Z_out[6]));
  Button N (.out(Z_out[5]));
  Button clear_Temp (.out(clear_Temp_out));
  Button O (.out(P_out[1]));
  Button P (.out(P_out[0]));
  Button K (.out(L_out[1]));
  Button L (.out(L_out[0]));
  _7_Segment_Display u_7_segment_display_1 (
    .g(main_2_out4), .f(main_2_out5), .a(main_2_out6), .b(main_2_out7), .e(main_2_out3), .d(main_2_out2),
    .c(main_2_out1), .dp(main_2_out0));
  _4BitDispalyer_main main_2 (
    .in(DataPath_win_out), .out7(main_2_out7), .out6(main_2_out6), .out5(main_2_out5), .out4(main_2_out4),
    .out3(main_2_out3), .out2(main_2_out2), .out1(main_2_out1), .out0(main_2_out0));
  Button run (.out(run_out));
  DataPath_main DataPath (
    .char_W(main_1_theoutput), .shift_W(main_1_outputavailable), .getWord(ControlUnit_getword),
    .clear_W(clear_Word_out), .set_W(1'b0), .load_i(ControlUnit_load_i), .count_i(ControlUnit_count_i),
    .clear_i(ControlUnit_clear_i), .load_nOc(ControlUnit_clear_noc), .nOc_in(in_2), .load_f(1'b0),
    .f_in(in_3), .count_f(ControlUnit_count_f), .clear_f(ControlUnit_clear_f), .ToPrint(ControlUnit_toprint),
    .StarToTemp(ControlUnit_startotemp), .clear_T(clear_Temp_out), .set_T(ControlUnit_set_t),
    .L_mistake(1'b0), .mistake_in(in_4), .count_mistake(ControlUnit_count_mistake),
    .clear_mistake(ControlUnit_clear_mistake), .L_win(1'b0), .win_in(in_5), .count_win(ControlUnit_countwin),
    .clear_win(clear_Win_out), .L_lost(1'b0), .lost_in(in_6), .count_lost(ControlUnit_countlost),
    .clear_lsot(clear_Lost_out), .isFound(ControlUnit_isfound_2), .isFound_en(ControlUnit_isfound_en),
    .isFound_clear(ControlUnit_isfound_clear), .CLK(clock_1_out), .input_eq_word_i(DataPath_input_eq_word_i),
    .i_gt_0(DataPath_i_gt_0), .i_eq_0(DataPath_i_eq_0), .i_lt_0(DataPath_i_lt_0),
    .i_gt_nOc(DataPath_i_gt_noc), .i_eq_nOc(DataPath_i_eq_noc), .i_lt_nOc(DataPath_i_lt_noc),
    .numberOfChar(DataPath_numberofchar), .nOc_eq_f(DataPath_noc_eq_f),
    .selectedToPrint(DataPath_selectedtoprint), .mistake_eq_10(DataPath_mistake_eq_10),
    .mistakes(DataPath_mistakes), .win_out(DataPath_win_out), .lost_out(DataPath_lost_out),
    .isFound_out(DataPath_isfound_out));  // open: word_i, nOc_gt_f, nOc_lt_f, temp_i, mistake_gt_10, mistake_lt_10
  _7_Segment_Display u_7_segment_display_2 (
    .g(main_3_out4), .f(main_3_out5), .a(main_3_out6), .b(main_3_out7), .e(main_3_out3), .d(main_3_out2),
    .c(main_3_out1), .dp(main_3_out0));
  _4BitDispalyer_main main_3 (
    .in(DataPath_numberofchar), .out7(main_3_out7), .out6(main_3_out6), .out5(main_3_out5),
    .out4(main_3_out4), .out3(main_3_out3), .out2(main_3_out2), .out1(main_3_out1), .out0(main_3_out0));
  _4BitDispalyer_main main_4 (
    .in(DataPath_lost_out), .out7(main_4_out7), .out6(main_4_out6), .out5(main_4_out5), .out4(main_4_out4),
    .out3(main_4_out3), .out2(main_4_out2), .out1(main_4_out1), .out0(main_4_out0));
  Button \new  (.out(new_out));
  _7_Segment_Display u_7_segment_display_3 (
    .g(main_4_out4), .f(main_4_out5), .a(main_4_out6), .b(main_4_out7), .e(main_4_out3), .d(main_4_out2),
    .c(main_4_out1), .dp(main_4_out0));
  TTY tty_1 (
    .data(bit_extender_1_out), .clk(clock_1_out), .we(ControlUnit_printavailable),
    .clr(ControlUnit_clearscreen));
  Bit_Extender #(.out_width(7)) bit_extender_1 (.in(DataPath_selectedtoprint), .out(bit_extender_1_out));
  ControlUnit_main ControlUnit (
    .input_eq_word_i(DataPath_input_eq_word_i), .i_gt_0(DataPath_i_gt_0), .i_eq_0(DataPath_i_eq_0),
    .i_lt_0(DataPath_i_lt_0), .i_gt_nOc(DataPath_i_gt_noc), .i_eq_nOc(DataPath_i_eq_noc),
    .i_lt_nOc(DataPath_i_lt_noc), .nOc_eq_f(DataPath_noc_eq_f), .mistake_eq_10(DataPath_mistake_eq_10),
    .isFound(DataPath_isfound_out), .scan(main_1_outputavailable), .run(run_out), .\new (new_out),
    .CLK(clock_1_out), .getWord(ControlUnit_getword), .clear_i(ControlUnit_clear_i),
    .clear_f(ControlUnit_clear_f), .clear_mistake(ControlUnit_clear_mistake),
    .isFound_clear(ControlUnit_isfound_clear), .starToTemp(ControlUnit_startotemp),
    .set_T(ControlUnit_set_t), .count_i(ControlUnit_count_i), .scan_Led(ControlUnit_scan_led),
    .isFound_en(ControlUnit_isfound_en), .count_f(ControlUnit_count_f), .isFound_2(ControlUnit_isfound_2),
    .count_i_2(ControlUnit_count_i), .count_mistake(ControlUnit_count_mistake), .load_i(ControlUnit_load_i),
    .clearScreen(ControlUnit_clearscreen), .printAvailable(ControlUnit_printavailable),
    .ToPrint(ControlUnit_toprint), .countWin(ControlUnit_countwin), .countLost(ControlUnit_countlost),
    .clear_nOc(ControlUnit_clear_noc));
  LED scan (.in(ControlUnit_scan_led));
  mistakes_main main_5 (
    .in(DataPath_mistakes), ._0(main_5__0), ._1(main_5__1), ._2(main_5__2), ._3(main_5__3), ._4(main_5__4),
    ._5(main_5__5), ._6(main_5__6), ._7(main_5__7), ._8(main_5__8), ._9(main_5__9));  // open: _10
  LED led_1 (.in(main_5__0));
  LED led_2 (.in(main_5__1));
  LED led_3 (.in(main_5__2));
  LED led_4 (.in(main_5__3));
  LED led_5 (.in(main_5__4));
  LED led_6 (.in(main_5__5));
  LED led_7 (.in(main_5__6));
  LED led_8 (.in(main_5__7));
  LED led_9 (.in(main_5__8));
  LED led_10 (.in(main_5__9));

  // Notes on the sheet:
  //   win
  //   numberOfChar
  //   lost
  //   mistakes
endmodule
