// Logisim project buttonHandler.circ as structural Verilog: 1 circuit, main circuit main
module main (
  input  Button_in,
  input  CLK,
  output Button_out
);

  wire and_3_out, and_4_out, not_1_out, not_2_out, not_3_out, not_4_out, not_5_out;
  wire [1:0] and_2_out, register_1_q;

  not not_1 (not_1_out, register_1_q[1]);
  and and_1 (Button_out, not_1_out, register_1_q[0]);
  and and_2 (and_2_out[0], Button_in, not_2_out, not_3_out);
  not not_2 (not_2_out, register_1_q[1]);
  not not_3 (not_3_out, register_1_q[0]);
  not not_4 (not_4_out, register_1_q[1]);
  and and_3 (and_3_out, Button_in, not_4_out, register_1_q[0]);
  and and_4 (and_4_out, Button_in, register_1_q[1], not_5_out);
  not not_5 (not_5_out, register_1_q[0]);
  Register #(.width(2)) register_1 (.D(and_2_out), .en(1'b1), .Q(register_1_q), .clk(CLK));  // open: clr
  or or_1 (and_2_out[1], and_3_out, and_4_out);
endmodule
