// Logisim project mistakes.circ as structural Verilog: 1 circuit, main circuit main
module main (
  input  [3:0] in,
  output _0,
  output _1,
  output _2,
  output _3,
  output _4,
  output _5,
  output _6,
  output _7,
  output _8,
  output _9,
  output _10
);

  Multiplexer #(.select(4), .width(11), .enable("false")) multiplexer_1 (
    .in0({11{1'b0}}), .in1(11'h1), .in2(11'h3), .in3(11'h7), .in4(11'hf), .in5(11'h1f), .in6(11'h3f),
    .in7(11'h7f), .in8(11'hff), .in9(11'h1ff), .in10(11'h3ff), .in11({11{1'b0}}), .in12({11{1'b0}}),
    .in13({11{1'b0}}), .in14({11{1'b0}}), .in15({11{1'b0}}),
    .out({_10, _9, _8, _7, _6, _5, _4, _3, _2, _1, _0}), .sel(in));
endmodule
