// Logisim project n0.circ as structural Verilog
module No (
  input  s0,
  input  s1,
  input  s2,
  input  s3,
  input  s4,
  input  run,
  input  i_lt_nOc,
  input  i_eq_nOc,
  input  i_gt_nOc,
  input  input_eq_word,
  input  isFound,
  input  mistake_eq_10,
  input  nOc_eq_f,
  input  scan,
  input  \new ,
  output n0
);

  wire and_1_out, and_2_out, and_3_out, and_4_out, and_5_out, and_6_out, and_7_out, and_8_out, and_9_out,
       nn0_1_n0, not_1_out, not_2_out, not_3_out, not_4_out, not_5_out, not_6_out, not_7_out, not_8_out,
       not_9_out, not_10_out, not_11_out, not_12_out, not_13_out, not_14_out, not_15_out, not_16_out,
       not_17_out, not_18_out, not_19_out, not_20_out, not_21_out, not_22_out, not_23_out, not_24_out,
       not_25_out, not_26_out, not_27_out, or_1_out, or_2_out, or_3_out;

  not not_1 (not_1_out, s0);
  not not_2 (not_2_out, s1);
  not not_3 (not_3_out, s2);
  not not_4 (not_4_out, s3);
  not not_5 (not_5_out, s4);
  not not_6 (not_6_out, s0);
  not not_7 (not_7_out, s2);
  not not_8 (not_8_out, s3);
  not not_9 (not_9_out, s4);
  or or_1 (or_1_out, i_lt_nOc, i_eq_nOc, i_gt_nOc);
  not not_10 (not_10_out, s3);
  not not_11 (not_11_out, s4);
  or or_2 (or_2_out, i_eq_nOc, i_gt_nOc);
  not not_12 (not_12_out, s0);
  not not_13 (not_13_out, s1);
  not not_14 (not_14_out, s2);
  not not_15 (not_15_out, s4);
  not not_16 (not_16_out, s2);
  not not_17 (not_17_out, s4);
  not not_18 (not_18_out, s0);
  not not_19 (not_19_out, s2);
  not not_20 (not_20_out, s3);
  not not_21 (not_21_out, mistake_eq_10);
  and and_1 (and_1_out, not_21_out, nOc_eq_f);
  not not_22 (not_22_out, s1);
  not not_23 (not_23_out, s3);
  not not_24 (not_24_out, s4);
  not not_25 (not_25_out, scan);
  not not_26 (not_26_out, s0);
  not not_27 (not_27_out, s2);
  and and_2 (and_2_out, not_1_out, not_2_out, not_3_out, not_4_out, not_5_out, run);
  and and_3 (and_3_out, not_6_out, s1, not_7_out, not_8_out, not_9_out, or_1_out);
  and and_4 (and_4_out, s0, s1, s2, not_10_out, not_11_out, or_2_out);
  and and_5 (and_5_out, not_12_out, not_13_out, not_14_out, s3, not_15_out, input_eq_word);
  and and_6 (and_6_out, s0, s1, not_16_out, s3, not_17_out, isFound);
  and and_7 (and_7_out, not_18_out, s1, not_19_out, not_20_out, s4, and_1_out);
  and and_8 (and_8_out, s0, not_22_out, s2, not_23_out, not_24_out, not_25_out);
  and and_9 (and_9_out, not_26_out, s1, not_27_out, s3, s4, \new );
  nn0 nn0_1 (.s4(s4), .s3(s3), .s2(s2), .s1(s1), .s0(s0), .n0(nn0_1_n0));
  or or_3 (or_3_out, and_2_out, and_3_out, and_4_out, and_5_out, and_6_out, and_7_out, and_8_out, and_9_out);
  or or_4 (n0, nn0_1_n0, or_3_out);
endmodule

module nn0 (
  input  s4,
  input  s3,
  input  s2,
  input  s1,
  input  s0,
  output n0
);

  wire and_1_out, and_2_out, and_3_out, and_4_out, and_5_out, and_6_out, not_1_out, not_2_out, not_3_out,
       not_4_out, not_5_out, not_6_out, not_7_out, not_8_out, not_9_out, not_10_out, not_11_out, not_12_out;

  not not_1 (not_1_out, s3);
  not not_2 (not_2_out, s0);
  not not_3 (not_3_out, s4);
  not not_4 (not_4_out, s0);
  not not_5 (not_5_out, s4);
  not not_6 (not_6_out, s0);
  not not_7 (not_7_out, s2);
  not not_8 (not_8_out, s1);
  not not_9 (not_9_out, s3);
  not not_10 (not_10_out, s2);
  not not_11 (not_11_out, s3);
  not not_12 (not_12_out, s0);
  and and_1 (and_1_out, not_1_out, s2, s1, not_2_out);
  and and_2 (and_2_out, not_3_out, s3, s1, not_4_out);
  and and_3 (and_3_out, not_5_out, s3, s2, not_6_out);
  and and_4 (and_4_out, s4, not_7_out, not_8_out);
  and and_5 (and_5_out, s4, not_9_out, not_10_out, s0);
  and and_6 (and_6_out, s4, not_11_out, s2, not_12_out);
  or or_1 (n0, and_1_out, and_2_out, and_3_out, and_4_out, and_5_out, and_6_out);
endmodule
