// Logisim project n1.circ as structural Verilog
module N1 (
  input  s4,
  input  s3,
  input  s2,
  input  s1,
  input  s0,
  input  scan,
  input  i_eq_noc,
  input  i_gt_noc,
  input  in_eq_word,
  input  i_lt_0,
  input  noc_eq_f,
  input  mistake_eq_10,
  input  i_lt_noc,
  output n1
);

  wire and_1_out, and_2_out, and_3_out, and_4_out, and_5_out, and_6_out, and_7_out, and_8_out, and_9_out,
       and_10_out, and_11_out, and_12_out, and_13_out, and_14_out, and_15_out, not_1_out, not_2_out,
       not_3_out, not_4_out, not_5_out, not_6_out, not_7_out, not_8_out, not_9_out, not_10_out, not_11_out,
       not_12_out, not_13_out, not_14_out, not_15_out, not_16_out, not_17_out, not_18_out, not_19_out,
       not_20_out, not_21_out, not_22_out, not_23_out, not_24_out, not_25_out, not_26_out, not_27_out,
       not_28_out, not_29_out, not_30_out, not_31_out, not_32_out, not_33_out, not_34_out, not_35_out,
       or_1_out, or_2_out, or_3_out;

  not not_1 (not_1_out, s2);
  not not_2 (not_2_out, s1);
  not not_3 (not_3_out, s4);
  not not_4 (not_4_out, s3);
  not not_5 (not_5_out, s0);
  not not_6 (not_6_out, s3);
  not not_7 (not_7_out, s0);
  not not_8 (not_8_out, s4);
  not not_9 (not_9_out, s1);
  not not_10 (not_10_out, s4);
  not not_11 (not_11_out, s0);
  not not_12 (not_12_out, s3);
  not not_13 (not_13_out, s1);
  not not_14 (not_14_out, s4);
  not not_15 (not_15_out, s3);
  not not_16 (not_16_out, s1);
  not not_17 (not_17_out, s4);
  not not_18 (not_18_out, s3);
  or or_1 (or_1_out, i_eq_noc, i_gt_noc);
  not not_19 (not_19_out, s4);
  not not_20 (not_20_out, s2);
  not not_21 (not_21_out, s1);
  not not_22 (not_22_out, s0);
  not not_23 (not_23_out, in_eq_word);
  not not_24 (not_24_out, s4);
  not not_25 (not_25_out, s3);
  not not_26 (not_26_out, s2);
  not not_27 (not_27_out, s0);
  and and_1 (and_1_out, noc_eq_f, not_28_out);
  not not_28 (not_28_out, mistake_eq_10);
  not not_29 (not_29_out, s3);
  not not_30 (not_30_out, s2);
  not not_31 (not_31_out, s0);
  not not_32 (not_32_out, s4);
  not not_33 (not_33_out, s3);
  not not_34 (not_34_out, s2);
  not not_35 (not_35_out, s0);
  and and_2 (and_2_out, not_1_out, not_2_out, s0);
  and and_3 (and_3_out, not_3_out, not_4_out, s2, not_5_out);
  and and_4 (and_4_out, not_6_out, s2, s1, not_7_out);
  and and_5 (and_5_out, not_8_out, s3, not_9_out, s0);
  and and_6 (and_6_out, not_10_out, s3, s1, not_11_out);
  and and_7 (and_7_out, s4, not_12_out, not_13_out, s0);
  and and_8 (and_8_out, not_14_out, not_15_out, s2, not_16_out, s0, scan);
  and and_9 (and_9_out, not_17_out, not_18_out, s2, s1, s0, or_1_out);
  and and_10 (and_10_out, not_19_out, s3, not_20_out, not_21_out, not_22_out, not_23_out);
  and and_11 (and_11_out, not_24_out, s3, s2, s1, s0, i_lt_0);
  and and_12 (and_12_out, s4, not_25_out, not_26_out, s1, not_27_out, and_1_out);
  and and_13 (and_13_out, s4, not_29_out, s2, s1, s0, i_lt_0);
  and and_14 (and_14_out, s4, s3, not_30_out, s1, not_31_out);
  and and_15 (and_15_out, not_32_out, not_33_out, not_34_out, s1, not_35_out, i_lt_noc);
  or or_2 (or_2_out, and_2_out, and_3_out, and_4_out, and_5_out, and_6_out, and_7_out);
  or or_3 (or_3_out, and_8_out, and_9_out, and_10_out, and_11_out, and_12_out, and_13_out, and_14_out, and_15_out);
  or or_4 (n1, or_2_out, or_3_out);
endmodule
