// Logisim project n2.circ as structural Verilog
module N2 (
  input  s4,
  input  s3,
  input  s2,
  input  s1,
  input  s0,
  input  i_eq_noc,
  input  i_gt_noc,
  input  noc_eq_f,
  input  mistake_eq_10,
  output n2
);

  wire and_1_out, and_2_out, and_3_out, and_4_out, and_5_out, and_6_out, and_7_out, and_8_out, and_9_out,
       and_10_out, and_11_out, not_1_out, not_2_out, not_3_out, not_4_out, not_5_out, not_6_out, not_7_out,
       not_8_out, not_9_out, not_10_out, not_11_out, not_12_out, not_13_out, not_14_out, not_15_out,
       not_16_out, not_17_out, not_18_out, not_19_out, not_20_out, not_21_out, not_22_out, not_23_out,
       not_24_out, or_1_out, or_2_out, or_3_out;

  not not_1 (not_1_out, s3);
  not not_2 (not_2_out, s2);
  not not_3 (not_3_out, s4);
  not not_4 (not_4_out, s1);
  not not_5 (not_5_out, s4);
  not not_6 (not_6_out, s0);
  not not_7 (not_7_out, s4);
  not not_8 (not_8_out, s2);
  not not_9 (not_9_out, s4);
  not not_10 (not_10_out, s1);
  not not_11 (not_11_out, s2);
  not not_12 (not_12_out, s1);
  not not_13 (not_13_out, s3);
  not not_14 (not_14_out, s1);
  not not_15 (not_15_out, s3);
  not not_16 (not_16_out, s0);
  not not_17 (not_17_out, s4);
  not not_18 (not_18_out, s3);
  not not_19 (not_19_out, s2);
  not not_20 (not_20_out, s0);
  or or_1 (or_1_out, i_eq_noc, i_gt_noc);
  not not_21 (not_21_out, s3);
  not not_22 (not_22_out, s2);
  not not_23 (not_23_out, s0);
  not not_24 (not_24_out, noc_eq_f);
  and and_1 (and_1_out, not_24_out, mistake_eq_10);
  and and_2 (and_2_out, not_1_out, not_2_out, s1, s0);
  and and_3 (and_3_out, not_3_out, s2, not_4_out, s0);
  and and_4 (and_4_out, not_5_out, s2, s1, not_6_out);
  and and_5 (and_5_out, not_7_out, s3, not_8_out, s1);
  and and_6 (and_6_out, not_9_out, s3, s2, not_10_out);
  and and_7 (and_7_out, s4, not_11_out, not_12_out, s0);
  and and_8 (and_8_out, s4, not_13_out, s2, not_14_out);
  and and_9 (and_9_out, s4, not_15_out, s2, not_16_out);
  and and_10 (and_10_out, not_17_out, not_18_out, not_19_out, s1, not_20_out, or_1_out);
  and and_11 (and_11_out, s4, not_21_out, not_22_out, s1, not_23_out, and_1_out);
  or or_2 (or_2_out, and_2_out, and_3_out, and_4_out, and_5_out, and_6_out, and_7_out, and_8_out, and_9_out);
  or or_3 (or_3_out, and_10_out, and_11_out);
  or or_4 (n2, or_2_out, or_3_out);
endmodule
