// Logisim project n3.circ as structural Verilog
module N3 (
  input  s4,
  input  s3,
  input  s2,
  input  s1,
  input  s0,
  output n3
);

  wire and_1_out, and_2_out, and_3_out, and_4_out, and_5_out, and_6_out, not_1_out, not_2_out, not_3_out,
       not_4_out, not_5_out, not_6_out, not_7_out, not_8_out, not_9_out, not_10_out, not_11_out, not_12_out;

  not not_1 (not_1_out, s3);
  not not_2 (not_2_out, s4);
  not not_3 (not_3_out, s1);
  not not_4 (not_4_out, s1);
  not not_5 (not_5_out, s2);
  not not_6 (not_6_out, s4);
  not not_7 (not_7_out, s0);
  not not_8 (not_8_out, s3);
  not not_9 (not_9_out, s2);
  not not_10 (not_10_out, s1);
  not not_11 (not_11_out, s2);
  not not_12 (not_12_out, s0);
  and and_1 (and_1_out, not_1_out, s2, s1, s0);
  and and_2 (and_2_out, not_2_out, s3, not_3_out);
  and and_3 (and_3_out, not_4_out, s3, not_5_out, s0);
  and and_4 (and_4_out, not_6_out, s3, s2, not_7_out);
  and and_5 (and_5_out, s4, not_8_out, not_9_out, not_10_out, s0);
  and and_6 (and_6_out, s4, s3, not_11_out, not_12_out);
  or or_1 (n3, and_1_out, and_2_out, and_3_out, and_4_out, and_5_out, and_6_out);
endmodule

module NN3 (
  input  s4,
  input  s3,
  input  s2,
  input  s1,
  input  s0,
  output n3
);

  wire and_1_out, and_2_out, and_3_out, and_4_out, and_5_out, and_6_out, not_1_out, not_2_out, not_3_out,
       not_4_out, not_5_out, not_6_out, not_7_out, not_8_out, not_9_out, not_10_out, not_11_out, not_12_out;

  not not_1 (not_1_out, s3);
  not not_2 (not_2_out, s4);
  not not_3 (not_3_out, s1);
  not not_4 (not_4_out, s4);
  not not_5 (not_5_out, s2);
  not not_6 (not_6_out, s4);
  not not_7 (not_7_out, s0);
  not not_8 (not_8_out, s3);
  not not_9 (not_9_out, s2);
  not not_10 (not_10_out, s1);
  not not_11 (not_11_out, s2);
  not not_12 (not_12_out, s0);
  and and_1 (and_1_out, not_1_out, s2, s1, s0);
  and and_2 (and_2_out, not_2_out, s3, not_3_out);
  and and_3 (and_3_out, not_4_out, s3, not_5_out, s0);
  and and_4 (and_4_out, not_6_out, s3, s2, not_7_out);
  and and_5 (and_5_out, s4, not_8_out, not_9_out, not_10_out, s0);
  and and_6 (and_6_out, s4, s3, not_11_out, not_12_out);
  or or_1 (n3, and_1_out, and_2_out, and_3_out, and_4_out, and_5_out, and_6_out);
endmodule
