// Logisim project n4.circ as structural Verilog
module N4 (
  input  s4,
  input  s3,
  input  s2,
  input  s1,
  input  s0,
  input  nOc_eq_f,
  input  mistake_eq_10,
  output n4
);

  wire and_1_out, and_2_out, and_3_out, and_4_out, and_5_out, and_6_out, and_7_out, not_1_out, not_2_out,
       not_3_out, not_4_out, not_5_out, not_6_out, not_7_out, not_8_out, not_9_out, not_10_out, not_11_out,
       not_12_out, not_13_out, xor_1_out;

  not not_1 (not_1_out, s4);
  not not_2 (not_2_out, s3);
  not not_3 (not_3_out, s1);
  not not_4 (not_4_out, s0);
  not not_5 (not_5_out, s3);
  not not_6 (not_6_out, s3);
  not not_7 (not_7_out, s2);
  not not_8 (not_8_out, s1);
  not not_9 (not_9_out, s2);
  not not_10 (not_10_out, s0);
  xor xor_1 (xor_1_out, nOc_eq_f, mistake_eq_10);
  and and_1 (and_1_out, not_1_out, s3, s2, s1, s0);
  and and_2 (and_2_out, s4, not_2_out, not_3_out, not_4_out);
  and and_3 (and_3_out, s4, not_5_out, s1, s0);
  and and_4 (and_4_out, s4, not_6_out, s2);
  and and_5 (and_5_out, s4, s3, not_7_out, not_8_out);
  and and_6 (and_6_out, s4, s3, not_9_out, not_10_out);
  not not_11 (not_11_out, s3);
  not not_12 (not_12_out, s2);
  and and_7 (and_7_out, s4, not_11_out, not_12_out, s1, not_13_out, xor_1_out);
  not not_13 (not_13_out, s0);
  or or_1 (n4, and_1_out, and_2_out, and_3_out, and_4_out, and_5_out, and_6_out, and_7_out);
endmodule
