// Logisim project staticArray.circ as structural Verilog: 1 circuit, main circuit main
module main (
  input  [7:0] \input ,
  input  shift,
  input  CLK,
  input  clear,
  input  [2:0] index,
  input  set,
  output [7:0] out
);

  wire multiplexer_1_out, multiplexer_4_out, multiplexer_7_out, multiplexer_11_out, multiplexer_13_out,
       multiplexer_18_out, multiplexer_21_out, multiplexer_25_out;
  wire [7:0] char0_q, char1_q, char2_q, char3_q, char4_q, char5_q, char6_q, char7_q, multiplexer_2_out,
       multiplexer_3_out, multiplexer_5_out, multiplexer_6_out, multiplexer_8_out, multiplexer_9_out,
       multiplexer_10_out, multiplexer_12_out, multiplexer_14_out, multiplexer_16_out, multiplexer_17_out,
       multiplexer_19_out, multiplexer_20_out, multiplexer_22_out, multiplexer_23_out, multiplexer_24_out,
       multiplexer_26_out;

  Multiplexer #(.enable("false")) multiplexer_1 (
    .in0(1'b0), .in1(multiplexer_16_out[7]), .out(multiplexer_1_out), .sel(set));
  Multiplexer #(.width(8), .enable("false")) multiplexer_2 (
    .in0(char7_q), .in1(\input ), .out(multiplexer_2_out), .sel(multiplexer_1_out));
  Multiplexer #(.width(8), .enable("false")) multiplexer_3 (
    .in0(multiplexer_2_out), .in1(char6_q), .out(multiplexer_3_out), .sel(shift));
  Register char7 (.D(multiplexer_3_out), .en(1'b1), .Q(char7_q), .clk(CLK), .clr(clear));
  Multiplexer #(.enable("false")) multiplexer_4 (
    .in0(1'b0), .in1(multiplexer_16_out[6]), .out(multiplexer_4_out), .sel(set));
  Multiplexer #(.width(8), .enable("false")) multiplexer_5 (
    .in0(char6_q), .in1(\input ), .out(multiplexer_5_out), .sel(multiplexer_4_out));
  Multiplexer #(.width(8), .enable("false")) multiplexer_6 (
    .in0(multiplexer_5_out), .in1(char5_q), .out(multiplexer_6_out), .sel(shift));
  Register char6 (.D(multiplexer_6_out), .en(1'b1), .Q(char6_q), .clk(CLK), .clr(clear));
  Multiplexer #(.enable("false")) multiplexer_7 (
    .in0(1'b0), .in1(multiplexer_16_out[5]), .out(multiplexer_7_out), .sel(set));
  Multiplexer #(.width(8), .enable("false")) multiplexer_8 (
    .in0(multiplexer_9_out), .in1(char4_q), .out(multiplexer_8_out), .sel(shift));
  Multiplexer #(.width(8), .enable("false")) multiplexer_9 (
    .in0(char5_q), .in1(\input ), .out(multiplexer_9_out), .sel(multiplexer_7_out));
  Register char5 (.D(multiplexer_8_out), .en(1'b1), .Q(char5_q), .clk(CLK), .clr(clear));
  Multiplexer #(.width(8), .enable("false")) multiplexer_10 (
    .in0(char4_q), .in1(\input ), .out(multiplexer_10_out), .sel(multiplexer_11_out));
  Multiplexer #(.enable("false")) multiplexer_11 (
    .in0(1'b0), .in1(multiplexer_16_out[4]), .out(multiplexer_11_out), .sel(set));
  Multiplexer #(.width(8), .enable("false")) multiplexer_12 (
    .in0(multiplexer_10_out), .in1(char3_q), .out(multiplexer_12_out), .sel(shift));
  Register char4 (.D(multiplexer_12_out), .en(1'b1), .Q(char4_q), .clk(CLK), .clr(clear));
  Multiplexer #(.enable("false")) multiplexer_13 (
    .in0(1'b0), .in1(multiplexer_16_out[3]), .out(multiplexer_13_out), .sel(set));
  Multiplexer #(.width(8), .enable("false")) multiplexer_14 (
    .in0(char3_q), .in1(\input ), .out(multiplexer_14_out), .sel(multiplexer_13_out));
  Multiplexer #(.select(3), .width(8), .enable("false")) multiplexer_15 (
    .in0(char0_q), .in1(char1_q), .in2(char2_q), .in3(char3_q), .in4(char4_q), .in5(char5_q), .in6(char6_q),
    .in7(char7_q), .out(out), .sel(index));
  Multiplexer #(.select(3), .width(8), .enable("false")) multiplexer_16 (
    .in0(8'h1), .in1(8'h2), .in2(8'h4), .in3(8'h8), .in4(8'h10), .in5(8'h20), .in6(8'h40), .in7(8'h80),
    .out(multiplexer_16_out), .sel(index));
  Multiplexer #(.width(8), .enable("false")) multiplexer_17 (
    .in0(multiplexer_14_out), .in1(char2_q), .out(multiplexer_17_out), .sel(shift));
  Register char3 (.D(multiplexer_17_out), .en(1'b1), .Q(char3_q), .clk(CLK), .clr(clear));
  Multiplexer #(.enable("false")) multiplexer_18 (
    .in0(1'b0), .in1(multiplexer_16_out[2]), .out(multiplexer_18_out), .sel(set));
  Multiplexer #(.width(8), .enable("false")) multiplexer_19 (
    .in0(char2_q), .in1(\input ), .out(multiplexer_19_out), .sel(multiplexer_18_out));
  Multiplexer #(.width(8), .enable("false")) multiplexer_20 (
    .in0(multiplexer_19_out), .in1(char1_q), .out(multiplexer_20_out), .sel(shift));
  Register char2 (.D(multiplexer_20_out), .en(1'b1), .Q(char2_q), .clk(CLK), .clr(clear));
  Multiplexer #(.enable("false")) multiplexer_21 (
    .in0(1'b0), .in1(multiplexer_16_out[1]), .out(multiplexer_21_out), .sel(set));
  Multiplexer #(.width(8), .enable("false")) multiplexer_22 (
    .in0(multiplexer_23_out), .in1(char0_q), .out(multiplexer_22_out), .sel(shift));
  Multiplexer #(.width(8), .enable("false")) multiplexer_23 (
    .in0(char1_q), .in1(\input ), .out(multiplexer_23_out), .sel(multiplexer_21_out));
  Register char1 (.D(multiplexer_22_out), .en(1'b1), .Q(char1_q), .clk(CLK), .clr(clear));
  Multiplexer #(.width(8), .enable("false")) multiplexer_24 (
    .in0(char0_q), .in1(\input ), .out(multiplexer_24_out), .sel(multiplexer_25_out));
  Multiplexer #(.enable("false")) multiplexer_25 (
    .in0(1'b0), .in1(multiplexer_16_out[0]), .out(multiplexer_25_out), .sel(set));
  Multiplexer #(.width(8), .enable("false")) multiplexer_26 (
    .in0(multiplexer_24_out), .in1(\input ), .out(multiplexer_26_out), .sel(shift));
  Register char0 (.D(multiplexer_26_out), .en(1'b1), .Q(char0_q), .clk(CLK), .clr(clear));
endmodule
