// Logisim project 171044066.circ as structural Verilog: 1 circuit, main circuit main
module main (
);

  wire and_1_out, and_4_out, and_7_out, and_8_out, and_9_out, and_10_out, and_11_out, and_12_out, and_13_out,
       and_14_out, and_15_out, and_16_out, and_17_out, and_18_out, and_19_out, and_20_out, and_21_out,
       and_22_out, and_23_out, and_24_out, and_25_out, and_26_out, and_27_out, and_28_out, and_29_out,
       and_30_out, and_31_out, button_1_out, button_2_out, button_3_out, clock_1_out, not_1_out, not_2_out,
       not_3_out, not_4_out, not_5_out, not_6_out, not_7_out, not_8_out, not_9_out, not_10_out, not_11_out,
       not_12_out, not_13_out, not_14_out, not_15_out, not_16_out, not_17_out, not_18_out, not_19_out,
       not_20_out, not_21_out, not_22_out, not_23_out, not_24_out, not_25_out, not_26_out, not_27_out,
       not_28_out, not_29_out, not_30_out, not_31_out, not_32_out, not_33_out, not_34_out, not_35_out,
       not_36_out, not_37_out, not_38_out, not_39_out, not_40_out, not_41_out, not_42_out, not_43_out,
       not_44_out, not_45_out, not_46_out, not_47_out, not_48_out, not_49_out, not_50_out, not_51_out,
       not_52_out, not_53_out, not_54_out, not_55_out, or_1_out, or_2_out, or_3_out, or_4_out, xor_1_out,
       xor_2_out;
  wire [1:0] and_3_out, and_6_out, register_1_q, register_2_q;
  wire [2:0] and_34_out, register_3_q;

  Button button_1 (.out(button_1_out));
  Button button_2 (.out(button_2_out));
  Clock clock_1 (.out(clock_1_out));
  Register #(.width(2)) register_1 (.D(and_3_out), .en(1'b1), .Q(register_1_q), .clk(clock_1_out));  // open: clr
  Register #(.width(2)) register_2 (.D(and_6_out), .en(1'b1), .Q(register_2_q), .clk(clock_1_out));  // open: clr
  not not_1 (not_1_out, register_2_q[0]);
  not not_2 (not_2_out, button_1_out);
  not not_3 (not_3_out, register_2_q[1]);
  not not_4 (not_4_out, register_2_q[1]);
  not not_5 (not_5_out, register_1_q[0]);
  and and_1 (and_1_out, not_5_out, register_1_q[1]);
  not not_6 (not_6_out, button_2_out);
  and and_2 (and_3_out[1], not_6_out, not_7_out, register_1_q[0]);
  not not_7 (not_7_out, register_1_q[1]);
  and and_3 (and_3_out[0], button_2_out, not_8_out);
  not not_8 (not_8_out, register_1_q[1]);
  and and_4 (and_4_out, not_1_out, register_2_q[1]);
  and and_5 (and_6_out[1], not_2_out, not_3_out, register_2_q[0]);
  and and_6 (and_6_out[0], button_1_out, not_4_out);
  not not_9 (not_9_out, register_3_q[2]);
  and and_7 (and_7_out, not_9_out, register_3_q[1], register_3_q[0]);
  LED led_1 (.in(and_7_out));
  not not_10 (not_10_out, register_3_q[2]);
  and and_8 (and_8_out, not_10_out, register_3_q[1], not_11_out);
  LED led_2 (.in(and_8_out));
  not not_11 (not_11_out, register_3_q[0]);
  not not_12 (not_12_out, register_3_q[2]);
  and and_9 (and_9_out, not_12_out, not_13_out, register_3_q[0]);
  LED led_3 (.in(and_9_out));
  not not_13 (not_13_out, register_3_q[1]);
  not not_14 (not_14_out, register_3_q[2]);
  and and_10 (and_10_out, not_14_out, not_15_out, not_16_out);
  not not_15 (not_15_out, register_3_q[1]);
  LED led_4 (.in(and_10_out));
  not not_16 (not_16_out, register_3_q[0]);
  LED led_5 (.in(and_11_out));
  not not_17 (not_17_out, register_3_q[1]);
  and and_11 (and_11_out, register_3_q[2], not_17_out, not_18_out);
  not not_18 (not_18_out, register_3_q[0]);
  and and_12 (and_12_out, register_3_q[2], not_19_out, register_3_q[0]);
  LED led_6 (.in(and_12_out));
  not not_19 (not_19_out, register_3_q[1]);
  and and_13 (and_13_out, register_3_q[2], register_3_q[1], not_20_out);
  LED led_7 (.in(and_13_out));
  not not_20 (not_20_out, register_3_q[0]);
  Button button_3 (.out(button_3_out));
  not not_21 (not_21_out, button_3_out);
  Register #(.width(3)) register_3 (.D(and_34_out), .en(1'b1), .Q(register_3_q), .clk(clock_1_out));  // open: clr
  not not_22 (not_22_out, register_3_q[0]);
  not not_23 (not_23_out, and_4_out);
  not not_24 (not_24_out, and_1_out);
  not not_25 (not_25_out, register_3_q[1]);
  not not_26 (not_26_out, and_4_out);
  not not_27 (not_27_out, register_3_q[1]);
  not not_28 (not_28_out, register_3_q[1]);
  not not_29 (not_29_out, and_4_out);
  not not_30 (not_30_out, register_3_q[2]);
  not not_31 (not_31_out, register_3_q[0]);
  not not_32 (not_32_out, and_1_out);
  not not_33 (not_33_out, register_3_q[2]);
  not not_34 (not_34_out, register_3_q[0]);
  not not_35 (not_35_out, register_3_q[2]);
  not not_36 (not_36_out, register_3_q[0]);
  not not_37 (not_37_out, and_4_out);
  not not_38 (not_38_out, register_3_q[1]);
  not not_39 (not_39_out, and_4_out);
  not not_40 (not_40_out, and_1_out);
  not not_41 (not_41_out, register_3_q[2]);
  not not_42 (not_42_out, register_3_q[0]);
  not not_43 (not_43_out, register_3_q[2]);
  not not_44 (not_44_out, and_1_out);
  not not_45 (not_45_out, register_3_q[2]);
  not not_46 (not_46_out, register_3_q[0]);
  not not_47 (not_47_out, register_3_q[1]);
  not not_48 (not_48_out, and_4_out);
  not not_49 (not_49_out, and_1_out);
  not not_50 (not_50_out, register_3_q[1]);
  and and_14 (and_14_out, register_3_q[2], register_3_q[1], not_22_out);
  and and_15 (and_15_out, not_23_out, not_24_out, register_3_q[2], not_25_out);
  and and_16 (and_16_out, not_26_out, and_1_out, register_3_q[2], not_27_out);
  and and_17 (and_17_out, and_4_out, and_1_out, register_3_q[2], not_28_out);
  and and_18 (and_18_out, not_29_out, and_1_out, not_30_out, not_31_out);
  and and_19 (and_19_out, and_4_out, not_32_out, register_3_q[2], register_3_q[0]);
  and and_20 (and_20_out, not_33_out, register_3_q[1], register_3_q[0]);
  and and_21 (and_21_out, register_3_q[2], register_3_q[1], not_34_out);
  and and_22 (and_22_out, and_4_out, not_35_out, register_3_q[1], not_36_out);
  xor xor_1 (xor_1_out, and_4_out, register_3_q[1]);
  and and_23 (and_23_out, not_37_out, and_1_out, register_3_q[2], not_38_out, register_3_q[0]);
  and and_24 (and_24_out, not_39_out, not_40_out, not_41_out, register_3_q[1], not_42_out);
  and and_25 (and_25_out, not_43_out, register_3_q[1], register_3_q[0]);
  and and_26 (and_26_out, and_4_out, not_44_out, not_45_out, not_46_out);
  and and_27 (and_27_out, and_4_out, and_1_out, not_47_out, register_3_q[0]);
  and and_28 (and_28_out, not_48_out, not_49_out, not_50_out, register_3_q[0]);
  xor xor_2 (xor_2_out, register_3_q[2], register_3_q[1]);
  or or_1 (or_1_out, and_18_out, and_19_out);
  not not_51 (not_51_out, register_3_q[1]);
  not not_52 (not_52_out, and_1_out);
  and and_29 (and_29_out, xor_1_out, not_52_out, not_53_out, register_3_q[0]);
  not not_53 (not_53_out, register_3_q[2]);
  not not_54 (not_54_out, and_4_out);
  not not_55 (not_55_out, register_3_q[0]);
  and and_30 (and_30_out, or_1_out, not_51_out);
  and and_31 (and_31_out, xor_2_out, not_54_out, and_1_out, not_55_out);
  or or_2 (or_2_out, and_14_out, and_15_out, and_16_out, and_17_out, and_30_out);
  or or_3 (or_3_out, and_20_out, and_21_out, and_22_out, and_29_out, and_23_out, and_24_out);
  or or_4 (or_4_out, and_25_out, and_26_out, and_27_out, and_28_out, and_31_out);
  and and_32 (and_34_out[2], or_2_out, not_21_out);
  and and_33 (and_34_out[1], or_3_out, not_21_out);
  and and_34 (and_34_out[0], or_4_out, not_21_out);

  // Notes on the sheet:
  //   B1
  //   B2
  //   L6
  //   L5
  //   L4
  //   L3
  //   L2
  //   L1
  //   L0
  //   Reset
  //   s2
  //   s0
  //   s1
  //   B1
  //   s0
  //   B2
  //   s1
  //   s2
endmodule
