// Logisim project ControlUnit.circ as structural Verilog: 1 circuit, main circuit main
module main (
  input  gt,
  input  eq,
  input  lt,
  input  signBit,
  input  Button,
  input  L_stateRegister,
  input  CLK,
  output load_A,
  output set_A,
  output neg_A,
  output load__B,
  output set_mult,
  output load_mult,
  output neg_mult,
  output signBitIn,
  output load_sign,
  output adder
);

  wire and_1_out, and_2_out, and_3_out, and_4_out, and_5_out, and_6_out, and_7_out, and_8_out, and_9_out,
       and_10_out, and_11_out, and_12_out, and_15_out, not_1_out, not_2_out, not_3_out, not_4_out, not_5_out,
       not_6_out, not_7_out, not_8_out, not_9_out, not_10_out, not_11_out, not_12_out, not_13_out,
       not_14_out, not_15_out, not_16_out, or_1_out, or_2_out, or_3_out, or_4_out, or_5_out, xor_1_out;
  wire [2:0] or_7_out, register_1_q;

  Register #(.width(3)) register_1 (.D(or_7_out), .en(L_stateRegister), .Q(register_1_q), .clk(CLK));  // open: clr
  and and_1 (and_1_out, signBit, eq);
  not not_1 (not_1_out, register_1_q[1]);
  and and_2 (and_2_out, not_1_out, Button);
  and and_3 (and_3_out, register_1_q[1], lt);
  and and_4 (and_4_out, register_1_q[2], eq, signBit);
  not not_2 (not_2_out, register_1_q[2]);
  and and_5 (and_5_out, not_2_out, register_1_q[1], not_3_out, lt);
  not not_3 (not_3_out, register_1_q[0]);
  or or_1 (or_1_out, gt, register_1_q[0]);
  not not_4 (not_4_out, register_1_q[2]);
  and and_6 (and_6_out, eq, signBit);
  or or_2 (or_2_out, and_6_out, gt);
  xor xor_1 (xor_1_out, register_1_q[1], register_1_q[0]);
  or or_3 (or_3_out, and_1_out, gt);
  not not_5 (not_5_out, register_1_q[1]);
  not not_6 (not_6_out, register_1_q[0]);
  or or_4 (or_4_out, and_2_out, and_3_out);
  not not_7 (not_7_out, register_1_q[2]);
  not not_8 (not_8_out, register_1_q[0]);
  or or_5 (or_5_out, and_4_out, register_1_q[0]);
  and and_7 (and_7_out, or_5_out, not_9_out);
  not not_9 (not_9_out, register_1_q[1]);
  and and_8 (and_8_out, or_1_out, not_4_out, register_1_q[1]);
  not not_10 (not_10_out, register_1_q[1]);
  not not_11 (not_11_out, register_1_q[0]);
  and and_9 (and_9_out, xor_1_out, register_1_q[2]);
  and and_10 (and_10_out, or_3_out, register_1_q[2], not_5_out, not_6_out);
  and and_11 (and_11_out, or_4_out, not_7_out, not_8_out);
  or or_6 (or_7_out[1], and_7_out, and_5_out);
  and and_12 (and_12_out, or_2_out, register_1_q[2], not_10_out, not_11_out);
  or or_7 (or_7_out[0], and_10_out, and_11_out);
  or or_8 (or_7_out[2], and_8_out, and_12_out, and_9_out);
  not not_12 (not_12_out, register_1_q[2]);
  not not_13 (not_13_out, register_1_q[1]);
  not not_14 (not_14_out, register_1_q[2]);
  not not_15 (not_15_out, register_1_q[1]);
  not not_16 (not_16_out, register_1_q[0]);
  and and_13 (load__B, not_12_out, not_13_out, register_1_q[0]);
  and and_14 (neg_A, not_14_out, register_1_q[1], register_1_q[0]);
  and and_15 (and_15_out, register_1_q[2], not_15_out, register_1_q[0]);
  and and_16 (adder, register_1_q[2], register_1_q[1], not_16_out);
  and and_17 (neg_mult, register_1_q[2], register_1_q[1], register_1_q[0]);
  or or_9 (load_A, load__B, neg_A, adder);
  or or_10 (set_A, neg_A, adder);
  or or_11 (set_mult, and_15_out, neg_mult);
  or or_12 (load_mult, load__B, and_15_out, neg_mult);
  or or_13 (load_sign, load__B, neg_A);

  assign signBitIn = neg_A;

  // Notes on the sheet:
  //   1
  //   3
  //   5
  //   6
  //   7
endmodule
