// Logisim project DataPath.circ as structural Verilog: 1 circuit, main circuit main
module main (
  input  [15:0] A_in,
  input  load_A,
  input  set_A,
  input  neg_A,
  input  adder,
  input  [15:0] B_in,
  input  load_B,
  input  [15:0] MinusOne,
  input  set_mult,
  input  [15:0] Zero16,
  input  load_mult,
  input  neg_mult,
  input  signBitIn,
  input  load_signBit,
  input  CLK,
  output gt_0,
  output eq_0,
  output lt_0,
  output [15:0] mult,
  output signBitOut
);

  wire [15:0] A_q, adder_1_out, B_q, multiplexer_1_out, multiplexer_2_out, multiplexer_3_out,
       multiplexer_4_out, multiplexer_5_out, multiplexer_6_out, negator_1_out, negator_2_out;

  Multiplexer #(.width(16), .enable("false")) multiplexer_1 (
    .in0(adder_1_out), .in1(negator_1_out), .out(multiplexer_1_out), .sel(neg_mult));
  Multiplexer #(.width(16), .enable("false")) multiplexer_2 (
    .in0(A_in), .in1(multiplexer_4_out), .out(multiplexer_2_out), .sel(set_A));
  Multiplexer #(.width(16), .enable("false")) multiplexer_3 (
    .in0(Zero16), .in1(multiplexer_1_out), .out(multiplexer_3_out), .sel(set_mult));
  Multiplexer #(.width(16), .enable("false")) multiplexer_4 (
    .in0(adder_1_out), .in1(negator_2_out), .out(multiplexer_4_out), .sel(neg_A));
  Negator #(.width(16)) negator_1 (.in(mult), .out(negator_1_out));
  Register #(.width(16)) A (.D(multiplexer_2_out), .en(load_A), .Q(A_q), .clk(CLK));  // open: clr
  Negator #(.width(16)) negator_2 (.in(A_q), .out(negator_2_out));
  Register #(.width(16)) B (.D(B_in), .en(load_B), .Q(B_q), .clk(CLK));  // open: clr
  Register #(.width(16)) u_mult (.D(multiplexer_3_out), .en(load_mult), .Q(mult), .clk(CLK));  // open: clr
  Register #(.width(1)) SignBit (.D(signBitIn), .en(load_signBit), .Q(signBitOut), .clk(CLK));  // open: clr
  Comparator #(.width(16)) comparator_1 (.a(A_q), .b(Zero16), .gt(gt_0), .eq(eq_0), .lt(lt_0));
  Multiplexer #(.width(16), .enable("false")) multiplexer_5 (
    .in0(mult), .in1(A_q), .out(multiplexer_5_out), .sel(adder));
  Multiplexer #(.width(16), .enable("false")) multiplexer_6 (
    .in0(B_q), .in1(MinusOne), .out(multiplexer_6_out), .sel(adder));
  Adder #(.width(16)) adder_1 (.a(multiplexer_5_out), .b(multiplexer_6_out), .out(adder_1_out));  // open: cin, cout
endmodule
