// Logisim project Main.circ as structural Verilog: 1 circuit, main circuit main
module main (
  input  [15:0] B,
  input  [15:0] A,
  output [15:0] \output 
);

  wire button_1_out, clock_1_out, main_1_adder, main_1_load__b, main_1_load_a, main_1_load_mult,
       main_1_load_sign, main_1_neg_a, main_1_neg_mult, main_1_set_a, main_1_set_mult, main_1_signbitin,
       main_2_eq_0, main_2_gt_0, main_2_lt_0, main_2_signbitout;

  Button button_1 (.out(button_1_out));
  Clock clock_1 (.out(clock_1_out));
  ControlUnit_main main_1 (
    .gt(main_2_gt_0), .eq(main_2_eq_0), .lt(main_2_lt_0), .signBit(main_2_signbitout), .Button(button_1_out),
    .L_stateRegister(1'b1), .CLK(clock_1_out), .load_A(main_1_load_a), .set_A(main_1_set_a),
    .neg_A(main_1_neg_a), .load__B(main_1_load__b), .set_mult(main_1_set_mult), .load_mult(main_1_load_mult),
    .neg_mult(main_1_neg_mult), .signBitIn(main_1_signbitin), .load_sign(main_1_load_sign),
    .adder(main_1_adder));
  DataPath_main main_2 (
    .A_in(A), .load_A(main_1_load_a), .set_A(main_1_set_a), .neg_A(main_1_neg_a), .adder(main_1_adder),
    .B_in(B), .load_B(main_1_load__b), .MinusOne({16{1'b1}}), .set_mult(main_1_set_mult),
    .Zero16({16{1'b0}}), .load_mult(main_1_load_mult), .neg_mult(main_1_neg_mult),
    .signBitIn(main_1_signbitin), .load_signBit(main_1_load_sign), .CLK(clock_1_out), .gt_0(main_2_gt_0),
    .eq_0(main_2_eq_0), .lt_0(main_2_lt_0), .mult(\output ), .signBitOut(main_2_signbitout));

  // Notes on the sheet:
  //   MinusOne_16bit
  //   Zero_16bit
endmodule
