// Logisim project 171044066_lab3.circ as structural Verilog: 1 circuit, main circuit main
module main (
  input  a,
  input  b
);

  wire and_1_out, and_2_out, and_3_out, and_4_out, and_5_out, and_6_out, and_7_out, and_8_out, and_9_out,
       clock_1_out, not_1_out, not_2_out, not_3_out, not_4_out, not_5_out, not_6_out, not_7_out, not_8_out,
       or_1_out, or_2_out, or_3_out;
  wire [1:0] or_4_out, register_1_q;

  Register #(.width(2)) register_1 (.D(or_4_out), .en(1'b1), .Q(register_1_q), .clk(clock_1_out));  // open: clr
  Clock clock_1 (.out(clock_1_out));
  and and_1 (and_1_out, register_1_q[0], register_1_q[1]);
  and and_2 (and_2_out, register_1_q[1], not_1_out);
  not not_1 (not_1_out, register_1_q[0]);
  and and_3 (and_3_out, register_1_q[1], not_2_out, b);
  not not_2 (not_2_out, a);
  not not_3 (not_3_out, register_1_q[1]);
  not not_4 (not_4_out, b);
  and and_4 (and_4_out, register_1_q[1], register_1_q[0], b);
  not not_5 (not_5_out, register_1_q[0]);
  not not_6 (not_6_out, a);
  and and_5 (and_5_out, not_5_out, not_6_out, not_7_out);
  not not_7 (not_7_out, b);
  and and_6 (and_6_out, not_3_out, not_4_out);
  or or_1 (or_1_out, and_6_out, and_4_out);
  not not_8 (not_8_out, register_1_q[1]);
  or or_2 (or_2_out, b, and_5_out);
  LED x (.in(or_3_out));
  or or_3 (or_3_out, and_1_out, and_2_out);
  and and_7 (and_7_out, a, or_1_out);
  and and_8 (and_8_out, not_8_out, register_1_q[0], a);
  and and_9 (and_9_out, register_1_q[1], or_2_out);
  or or_4 (or_4_out[0], and_3_out, and_7_out);
  or or_5 (or_4_out[1], and_8_out, and_9_out);
endmodule
