// Logisim project 171044066_lab4.circ as structural Verilog: 1 circuit, main circuit main
module main (
  input  req,
  input  p3s,
  input  p7s,
  input  p37s
);

  wire and_1_out, and_2_out, and_3_out, and_4_out, and_5_out, and_6_out, and_7_out, and_8_out, and_9_out,
       and_10_out, and_11_out, and_12_out, and_13_out, and_14_out, clock_1_out, not_1_out, not_2_out,
       not_3_out, not_4_out, not_5_out, not_6_out, not_7_out, not_8_out, not_9_out, not_10_out, not_11_out,
       not_12_out, not_13_out, not_14_out, or_1_out, or_2_out, or_3_out;
  wire [1:0] or_5_out, register_1_q;

  Register #(.width(2)) register_1 (.D(or_5_out), .en(1'b1), .Q(register_1_q), .clk(clock_1_out));  // open: clr
  Clock clock_1 (.out(clock_1_out));
  and and_1 (and_1_out, register_1_q[0], not_1_out);
  not not_1 (not_1_out, register_1_q[1]);
  not not_2 (not_2_out, register_1_q[0]);
  and and_2 (and_2_out, not_2_out, not_3_out);
  not not_3 (not_3_out, register_1_q[1]);
  not not_4 (not_4_out, register_1_q[0]);
  and and_3 (and_3_out, not_4_out, register_1_q[1]);
  and and_4 (and_4_out, register_1_q[0], register_1_q[1]);
  not not_5 (not_5_out, register_1_q[0]);
  and and_5 (and_5_out, not_5_out, not_6_out);
  not not_6 (not_6_out, register_1_q[1]);
  and and_6 (and_6_out, register_1_q[0], not_7_out);
  not not_7 (not_7_out, p37s);
  not not_8 (not_8_out, register_1_q[0]);
  and and_7 (and_7_out, not_8_out, p7s);
  and and_8 (and_8_out, register_1_q[0], not_9_out);
  not not_9 (not_9_out, p3s);
  not not_10 (not_10_out, register_1_q[0]);
  and and_9 (and_9_out, not_10_out, req);
  and and_10 (and_10_out, register_1_q[0], register_1_q[1], not_11_out);
  not not_11 (not_11_out, p37s);
  not not_12 (not_12_out, register_1_q[0]);
  and and_11 (and_11_out, not_12_out, register_1_q[1]);
  not not_13 (not_13_out, register_1_q[1]);
  and and_12 (and_12_out, register_1_q[0], not_13_out, p3s);
  or or_1 (or_1_out, and_1_out, and_2_out);
  or or_2 (or_2_out, and_6_out, and_7_out);
  or or_3 (or_3_out, and_8_out, and_9_out);
  and and_13 (and_13_out, register_1_q[1], or_2_out);
  not not_14 (not_14_out, register_1_q[1]);
  and and_14 (and_14_out, not_14_out, or_3_out);
  or or_4 (or_5_out[1], and_10_out, and_11_out, and_12_out);
  or or_5 (or_5_out[0], and_13_out, and_14_out);
  LED red (.in(or_1_out));
  LED orange (.in(and_3_out));
  LED green (.in(and_4_out));
  LED reset (.in(and_5_out));
endmodule
