// Logisim project Main.circ as structural Verilog: 1 circuit, main circuit main
module main (
  input  req,
  input  [7:0] initial_Time
);

  wire clock_1_out, main_1_e3, main_1_e7, main_1_e37, main_1_g3, main_1_g7, main_1_g37, main_2_green,
       main_2_orange, main_2_red, main_2_resett, or_1_out, or_2_out, or_3_out;
  wire [7:7] not_1_out;

  not not_1 (not_1_out[7], 1'b1);
  Clock clock_1 (.out(clock_1_out));
  datapath_main main_1 (
    .resetT(main_2_resett), .timer_init(initial_Time), ._3({{6{not_1_out[7]}}, 2'b11}), .L_time(1'b1),
    .CLK(clock_1_out), ._7({{5{not_1_out[7]}}, 3'b111}),
    ._37({{2{not_1_out[7]}}, 1'b1, {2{not_1_out[7]}}, 1'b1, not_1_out[7], 1'b1}), .g3(main_1_g3),
    .e3(main_1_e3), .g7(main_1_g7), .e7(main_1_e7), .g37(main_1_g37), .e37(main_1_e37));  // open: l3, l7, l37
  or or_1 (or_1_out, main_1_g3, main_1_e3);
  or or_2 (or_2_out, main_1_g7, main_1_e7);
  or or_3 (or_3_out, main_1_g37, main_1_e37);
  ControlUnit_main main_2 (
    .req(req), .p3s(or_1_out), .p7s(or_2_out), .p37s(or_3_out), .red(main_2_red), .orange(main_2_orange),
    .green(main_2_green), .resetT(main_2_resett));
  LED red (.in(main_2_red));
  LED orange (.in(main_2_orange));
  LED green (.in(main_2_green));
endmodule
