// Logisim project datapath.circ as structural Verilog: 1 circuit, main circuit main
module main (
  input  resetT,
  input  [7:0] timer_init,
  input  [7:0] _3,
  input  L_time,
  input  CLK,
  input  [7:0] _7,
  input  [7:0] _37,
  output g3,
  output e3,
  output l3,
  output g7,
  output e7,
  output l7,
  output g37,
  output e37,
  output l37
);

  wire not_2_out;
  wire [7:0] adder_1_out, multiplexer_1_out, time_q;
  wire [7:7] not_1_out;

  not not_1 (not_1_out[7], 1'b1);
  not not_2 (not_2_out, resetT);
  Multiplexer #(.width(8), .enable("false")) multiplexer_1 (
    .in0(timer_init), .in1(adder_1_out), .out(multiplexer_1_out), .sel(not_2_out));
  Register \time  (.D(multiplexer_1_out), .en(L_time), .Q(time_q), .clk(CLK));  // open: clr
  Adder adder_1 (.a(time_q), .b({{7{not_1_out[7]}}, 1'b1}), .out(adder_1_out));  // open: cin, cout
  Comparator comparator_1 (.a(time_q), .b(_3), .gt(g3), .eq(e3), .lt(l3));
  Comparator comparator_2 (.a(time_q), .b(_7), .gt(g7), .eq(e7), .lt(l7));
  Comparator comparator_3 (.a(time_q), .b(_37), .gt(g37), .eq(e37), .lt(l37));

  // Notes on the sheet:
  //   +1
endmodule
