// Logisim project ControlUnit.circ as structural Verilog: 1 circuit, main circuit main
module main (
  input  go,
  input  gt,
  input  CLK,
  output L_x,
  output L_y,
  output S_z,
  output L_z,
  output S_diff,
  output L_diff,
  output L_diff2
);

  wire and_1_out, and_2_out, and_3_out, and_4_out, and_5_out, and_6_out, and_7_out, and_8_out, and_9_out,
       and_10_out, and_12_out, not_1_out, not_2_out, not_3_out, not_4_out, not_5_out, not_6_out, not_7_out,
       not_8_out, not_9_out, not_10_out, not_11_out, not_12_out, not_13_out, not_14_out, not_15_out,
       not_16_out, not_17_out, not_18_out, not_19_out, not_20_out, not_21_out, or_2_out;
  wire [2:0] or_3_out, register_1_q;

  Register #(.width(3)) register_1 (.D(or_3_out), .en(1'b1), .Q(register_1_q), .clk(CLK));  // open: clr
  not not_1 (not_1_out, register_1_q[0]);
  and and_1 (and_1_out, not_1_out, register_1_q[1], not_2_out);
  not not_2 (not_2_out, register_1_q[2]);
  not not_3 (not_3_out, register_1_q[0]);
  not not_4 (not_4_out, register_1_q[1]);
  and and_2 (and_2_out, not_3_out, not_4_out, register_1_q[2], gt);
  not not_5 (not_5_out, register_1_q[0]);
  not not_6 (not_6_out, register_1_q[1]);
  and and_3 (and_3_out, not_5_out, not_6_out, not_7_out, go);
  not not_7 (not_7_out, register_1_q[2]);
  not not_8 (not_8_out, register_1_q[0]);
  and and_4 (and_4_out, not_8_out, register_1_q[1], not_9_out);
  not not_9 (not_9_out, register_1_q[2]);
  and and_5 (and_5_out, register_1_q[0], not_10_out);
  not not_10 (not_10_out, register_1_q[1]);
  and and_6 (and_6_out, gt, not_11_out);
  not not_11 (not_11_out, register_1_q[1]);
  not not_12 (not_12_out, register_1_q[0]);
  and and_7 (and_7_out, not_12_out, register_1_q[2]);
  not not_13 (not_13_out, register_1_q[1]);
  and and_8 (and_8_out, register_1_q[0], not_13_out, register_1_q[2]);
  and and_9 (and_9_out, register_1_q[0], register_1_q[1], not_14_out);
  not not_14 (not_14_out, register_1_q[2]);
  or or_1 (or_3_out[1], and_4_out, and_5_out);
  or or_2 (or_2_out, register_1_q[1], and_6_out);
  or or_3 (or_3_out[0], and_1_out, and_2_out, and_3_out);
  and and_10 (and_10_out, or_2_out, and_7_out);
  or or_4 (or_3_out[2], and_10_out, and_8_out, and_9_out);
  not not_15 (not_15_out, register_1_q[1]);
  not not_16 (not_16_out, register_1_q[2]);
  not not_17 (not_17_out, register_1_q[0]);
  not not_18 (not_18_out, register_1_q[2]);
  not not_19 (not_19_out, register_1_q[2]);
  not not_20 (not_20_out, register_1_q[1]);
  not not_21 (not_21_out, register_1_q[0]);
  and and_11 (L_x, register_1_q[0], not_15_out, not_16_out);
  and and_12 (and_12_out, not_17_out, register_1_q[1], not_18_out);
  and and_13 (L_diff2, register_1_q[0], register_1_q[1], not_19_out);
  and and_14 (S_z, register_1_q[0], not_20_out, register_1_q[2]);
  and and_15 (S_diff, not_21_out, register_1_q[1], register_1_q[2]);
  or or_5 (L_z, L_x, S_z);
  or or_6 (L_diff, and_12_out, S_diff);

  assign L_y = L_x;

  // Notes on the sheet:
  //   s1
  //   s2
  //   s0
endmodule
