// Logisim project DataPath.circ as structural Verilog: 1 circuit, main circuit main
// Z
module main (
  input  [7:0] x_i,
  input  [7:0] y_i,
  input  CLK,
  input  L_x,
  input  L_y,
  input  S_z,
  input  L_z,
  input  S_diff,
  input  L_diff,
  input  L_diff2,
  output [7:0] Z,
  output gt0,
  output eq0,
  output lt0
);

  wire [0:0] not_1_out;
  wire [7:0] diff2_q, diff_q, multiplexer_1_out, multiplexer_2_out, multiplier_1_out, subtractor_1_out,
       subtractor_2_out, X_q, Y_q;

  not not_1 (not_1_out[0], 1'b0);
  Multiplexer #(.width(8), .enable("false")) multiplexer_1 (
    .in0({{7{1'b0}}, not_1_out[0]}), .in1(multiplier_1_out), .out(multiplexer_1_out), .sel(S_z));
  Multiplexer #(.width(8), .enable("false")) multiplexer_2 (
    .in0(subtractor_2_out), .in1(subtractor_1_out), .out(multiplexer_2_out), .sel(S_diff));
  Register X (.D(x_i), .en(L_x), .Q(X_q), .clk(CLK));  // open: clr
  Register Y (.D(y_i), .en(L_y), .Q(Y_q), .clk(CLK));  // open: clr
  Register u_Z (.D(multiplexer_1_out), .en(L_z), .Q(Z), .clk(CLK));  // open: clr
  Register diff (.D(multiplexer_2_out), .en(L_diff), .Q(diff_q), .clk(CLK));  // open: clr
  Register diff2 (.D(diff_q), .en(L_diff2), .Q(diff2_q), .clk(CLK));  // open: clr
  Subtractor subtractor_1 (.a(diff_q), .b({{7{1'b0}}, not_1_out[0]}), .out(subtractor_1_out));  // open: bin, bout
  Subtractor subtractor_2 (.a(X_q), .b(Y_q), .out(subtractor_2_out));  // open: bin, bout
  Multiplier multiplier_1 (.a(Z), .b(diff2_q), .out(multiplier_1_out));  // open: cin, cout
  Comparator comparator_1 (.a(diff_q), .b({8{1'b0}}), .gt(gt0), .eq(eq0), .lt(lt0));

  // Notes on the sheet:
  //   X-Y
  //   Z * diff2
endmodule
