// Logisim project Main.circ as structural Verilog: 1 circuit, main circuit main
module main (
  input  go,
  input  [7:0] Y_i,
  input  [7:0] X_i,
  output [7:0] Z
);

  wire clock_1_out, main_1_l_diff, main_1_l_diff2, main_1_l_x, main_1_l_y, main_1_l_z, main_1_s_diff,
       main_1_s_z, main_2_gt0;

  Clock clock_1 (.out(clock_1_out));
  ControlUnit_main main_1 (
    .go(go), .gt(main_2_gt0), .CLK(clock_1_out), .L_x(main_1_l_x), .L_y(main_1_l_y), .S_z(main_1_s_z),
    .L_z(main_1_l_z), .S_diff(main_1_s_diff), .L_diff(main_1_l_diff), .L_diff2(main_1_l_diff2));
  DataPath_main main_2 (
    .x_i(X_i), .y_i(Y_i), .CLK(clock_1_out), .L_x(main_1_l_x), .L_y(main_1_l_y), .S_z(main_1_s_z),
    .L_z(main_1_l_z), .S_diff(main_1_s_diff), .L_diff(main_1_l_diff), .L_diff2(main_1_l_diff2), .Z(Z),
    .gt0(main_2_gt0));  // open: eq0, lt0
endmodule
