// Logisim project control.circ as structural Verilog: 1 circuit, main circuit main
module main (
  input  start,
  input  product0,
  input  done,
  input  enable_state_register,
  input  clear_state_register,
  input  CLK,
  output overflow_en,
  output overflow_clr,
  output init,
  output shift,
  output enable,
  output count
);

  wire and_1_out, and_2_out, and_3_out, and_4_out, and_5_out, and_6_out, and_7_out, and_8_out, and_9_out,
       and_10_out, and_11_out, not_1_out, not_2_out, not_3_out, not_4_out, not_5_out, not_6_out, not_7_out,
       not_8_out, not_9_out, not_10_out, not_11_out, not_12_out, not_13_out, not_14_out, not_15_out,
       not_16_out, not_17_out, not_18_out, not_19_out, not_20_out, not_21_out, or_1_out, or_2_out, or_3_out;
  wire [2:0] or_4_out, register_1_q;

  not not_1 (not_1_out, register_1_q[2]);
  not not_2 (not_2_out, register_1_q[0]);
  not not_3 (not_3_out, register_1_q[1]);
  not not_4 (not_4_out, register_1_q[0]);
  not not_5 (not_5_out, register_1_q[2]);
  not not_6 (not_6_out, done);
  not not_7 (not_7_out, register_1_q[1]);
  not not_8 (not_8_out, register_1_q[0]);
  not not_9 (not_9_out, register_1_q[1]);
  not not_10 (not_10_out, product0);
  not not_11 (not_11_out, register_1_q[0]);
  not not_12 (not_12_out, register_1_q[2]);
  Register #(.width(3)) register_1 (
    .D(or_4_out), .en(enable_state_register), .Q(register_1_q), .clk(CLK), .clr(clear_state_register));
  or or_1 (or_1_out, register_1_q[2], and_1_out);
  and and_1 (and_1_out, start, not_1_out);
  and and_2 (and_2_out, not_2_out, not_3_out);
  and and_3 (and_3_out, product0, not_4_out, register_1_q[1], not_5_out);
  not not_13 (not_13_out, register_1_q[2]);
  or or_2 (or_2_out, not_13_out, and_4_out);
  and and_4 (and_4_out, not_6_out, register_1_q[2]);
  and and_5 (and_5_out, register_1_q[0], not_7_out);
  and and_6 (and_6_out, not_8_out, not_9_out, register_1_q[2]);
  or or_3 (or_3_out, register_1_q[0], and_7_out);
  and and_7 (and_7_out, not_10_out, not_11_out);
  and and_8 (and_8_out, register_1_q[1], not_12_out);
  and and_9 (and_9_out, or_1_out, and_2_out);
  and and_10 (and_10_out, or_2_out, and_5_out);
  and and_11 (and_11_out, or_3_out, and_8_out);
  or or_4 (or_4_out[0], and_9_out, and_3_out);
  or or_5 (or_4_out[1], and_3_out, and_10_out);
  or or_6 (or_4_out[2], and_6_out, and_11_out);
  not not_14 (not_14_out, register_1_q[2]);
  and and_12 (init, not_14_out, not_15_out, register_1_q[0]);
  not not_15 (not_15_out, register_1_q[1]);
  not not_16 (not_16_out, register_1_q[2]);
  and and_13 (overflow_clr, not_16_out, register_1_q[1], not_17_out);
  not not_17 (not_17_out, register_1_q[0]);
  not not_18 (not_18_out, register_1_q[2]);
  and and_14 (overflow_en, not_18_out, register_1_q[1], register_1_q[0]);
  not not_19 (not_19_out, register_1_q[1]);
  and and_15 (shift, register_1_q[2], not_19_out, not_20_out);
  not not_20 (not_20_out, register_1_q[0]);
  not not_21 (not_21_out, register_1_q[1]);
  and and_16 (count, register_1_q[2], not_21_out, register_1_q[0]);
  or or_7 (enable, shift, overflow_en, init);
endmodule
