// Logisim project datapath.circ as structural Verilog: 5 circuits, main circuit main
module main (
  input  [31:0] Multiplicand,
  input  [31:0] Multiplier,
  input  overflow_en,
  input  overflow_clr,
  input  init,
  input  shift,
  input  enable,
  input  CLK,
  input  clear,
  input  count,
  output isOverFlow,
  output product0_isOne,
  output [31:0] Mostignificant,
  output [31:0] LeastSignificant,
  output is_done
);

  wire n32_bit_adder_1_c_i_1;
  wire [31:0] multiplexer_1_out, multiplexer_2_out, n32_bit_adder_1_r;

  _32_bit_adder u_32_bit_adder_1 (
    .A(Mostignificant), .C_i(1'b0), .B(Multiplicand), .C_i_1(n32_bit_adder_1_c_i_1), .R(n32_bit_adder_1_r));
  Multiplexer #(.width(32), .enable("false")) multiplexer_1 (
    .in0(n32_bit_adder_1_r), .in1({32{1'b0}}), .out(multiplexer_1_out), .sel(init));
  _64_bit_shift_register u_64_bit_shift_register_1 (
    .LeastSignificant32_In(multiplexer_2_out), .MostSignificant32_In(multiplexer_1_out), .Shift(shift),
    .Shift_Bit_In(isOverFlow), .Enable(enable), .CLK(CLK), .Clear(clear),
    .LeastSignificant32_Out(LeastSignificant), .MostSignificant32_Out(Mostignificant));  // open: Shift_Bit_Out
  Counter #(.width(5), .max('h1f)) counter_1 (
    .load(init), .D({5{1'b0}}), .count(count), .carry(is_done), .clk(CLK), .clr(1'b0));  // open: Q
  Multiplexer #(.width(32), .enable("false")) multiplexer_2 (
    .in0(LeastSignificant), .in1(Multiplier), .out(multiplexer_2_out), .sel(init));
  Register #(.width(1)) u_isOverFlow (
    .D(n32_bit_adder_1_c_i_1), .en(overflow_en), .Q(isOverFlow), .clk(CLK), .clr(overflow_clr));

  assign product0_isOne = LeastSignificant[0];

  // Notes on the sheet:
  //   Shift Bit
endmodule

module _64_bit_shift_register (
  input  [31:0] LeastSignificant32_In,
  input  [31:0] MostSignificant32_In,
  input  Shift,
  input  Shift_Bit_In,
  input  Enable,
  input  CLK,
  input  Clear,
  output Shift_Bit_Out,
  output [31:0] LeastSignificant32_Out,
  output [31:0] MostSignificant32_Out
);

  wire [31:0] multiplexer_1_out, multiplexer_2_out;

  Multiplexer #(.width(32), .enable("false")) multiplexer_1 (
    .in0(LeastSignificant32_In), .in1({MostSignificant32_Out[0], LeastSignificant32_Out[31:1]}),
    .out(multiplexer_1_out), .sel(Shift));
  Multiplexer #(.width(32), .enable("false")) multiplexer_2 (
    .in0(MostSignificant32_In), .in1({Shift_Bit_In, MostSignificant32_Out[31:1]}), .out(multiplexer_2_out),
    .sel(Shift));
  Register #(.width(32)) LeastSignificant32 (
    .D(multiplexer_1_out), .en(Enable), .Q(LeastSignificant32_Out), .clk(CLK), .clr(Clear));
  Register #(.width(32)) MostSignificant32 (
    .D(multiplexer_2_out), .en(Enable), .Q(MostSignificant32_Out), .clk(CLK), .clr(Clear));

  assign Shift_Bit_Out = LeastSignificant32_Out[0];
endmodule

module _1_bit_adder (
  input  A_i,
  input  B_i,
  input  C_i,
  output S_i,
  output C_i_1
);

  wire and_1_out, and_2_out, and_3_out, not_1_out, not_2_out, or_1_out, or_2_out;

  or or_1 (or_1_out, A_i, B_i);
  and and_1 (and_1_out, A_i, B_i);
  and and_2 (and_2_out, or_1_out, not_1_out);
  not not_1 (not_1_out, and_1_out);
  or or_2 (or_2_out, and_2_out, C_i);
  and and_3 (and_3_out, and_2_out, C_i);
  not not_2 (not_2_out, and_3_out);
  and and_4 (S_i, or_2_out, not_2_out);
  or or_3 (C_i_1, and_3_out, and_1_out);
endmodule

module _32_bit_adder_helper (
  input  c_i,
  input  A_MSB,
  input  A,
  input  A_2,
  input  A_3,
  input  A_4,
  input  A_5,
  input  A_6,
  input  A_7,
  input  A_8,
  input  A_9,
  input  A_10,
  input  A_11,
  input  A_12,
  input  A_13,
  input  A_14,
  input  A_15,
  input  A_16,
  input  A_17,
  input  A_18,
  input  A_19,
  input  A_20,
  input  A_21,
  input  A_22,
  input  A_23,
  input  A_24,
  input  A_25,
  input  A_26,
  input  A_27,
  input  A_28,
  input  A_29,
  input  A_30,
  input  A_31,
  input  B_MSB,
  input  B,
  input  B_2,
  input  B_3,
  input  B_4,
  input  B_5,
  input  B_6,
  input  B_7,
  input  B_8,
  input  B_9,
  input  B_10,
  input  B_11,
  input  B_12,
  input  B_13,
  input  B_14,
  input  B_15,
  input  B_16,
  input  B_17,
  input  B_18,
  input  B_19,
  input  B_20,
  input  B_21,
  input  B_22,
  input  B_23,
  input  B_24,
  input  B_25,
  input  B_26,
  input  B_27,
  input  B_28,
  input  B_29,
  input  B_30,
  input  B_31,
  output C_i_1,
  output S_i_MSB,
  output S_i,
  output S_i_2,
  output S_i_3,
  output S_i_4,
  output S_i_5,
  output S_i_6,
  output S_i_7,
  output S_i_8,
  output S_i_9,
  output S_i_10,
  output S_i_11,
  output S_i_12,
  output S_i_13,
  output S_i_14,
  output S_i_15,
  output S_i_16,
  output S_i_17,
  output S_i_18,
  output S_i_19,
  output S_i_20,
  output S_i_21,
  output S_i_22,
  output S_i_23,
  output S_i_24,
  output S_i_25,
  output S_i_26,
  output S_i_27,
  output S_i_28,
  output S_i_29,
  output S_i_30,
  output S_i_31
);

  wire n1_bit_adder_2_c_i_1, n1_bit_adder_3_c_i_1, n1_bit_adder_4_c_i_1, n1_bit_adder_5_c_i_1,
       n1_bit_adder_6_c_i_1, n1_bit_adder_7_c_i_1, n1_bit_adder_8_c_i_1, n1_bit_adder_9_c_i_1,
       n1_bit_adder_10_c_i_1, n1_bit_adder_11_c_i_1, n1_bit_adder_12_c_i_1, n1_bit_adder_13_c_i_1,
       n1_bit_adder_14_c_i_1, n1_bit_adder_15_c_i_1, n1_bit_adder_16_c_i_1, n1_bit_adder_17_c_i_1,
       n1_bit_adder_18_c_i_1, n1_bit_adder_19_c_i_1, n1_bit_adder_20_c_i_1, n1_bit_adder_21_c_i_1,
       n1_bit_adder_22_c_i_1, n1_bit_adder_23_c_i_1, n1_bit_adder_24_c_i_1, n1_bit_adder_25_c_i_1,
       n1_bit_adder_26_c_i_1, n1_bit_adder_27_c_i_1, n1_bit_adder_28_c_i_1, n1_bit_adder_29_c_i_1,
       n1_bit_adder_30_c_i_1, n1_bit_adder_31_c_i_1, n1_bit_adder_32_c_i_1;

  _1_bit_adder u_1_bit_adder_1 (.A_i(A_MSB), .B_i(B_MSB), .C_i(n1_bit_adder_2_c_i_1), .S_i(S_i_MSB), .C_i_1(C_i_1));
  _1_bit_adder u_1_bit_adder_2 (.A_i(A), .B_i(B), .C_i(n1_bit_adder_3_c_i_1), .S_i(S_i), .C_i_1(n1_bit_adder_2_c_i_1));
  _1_bit_adder u_1_bit_adder_3 (
    .A_i(A_2), .B_i(B_2), .C_i(n1_bit_adder_4_c_i_1), .S_i(S_i_2), .C_i_1(n1_bit_adder_3_c_i_1));
  _1_bit_adder u_1_bit_adder_4 (
    .A_i(A_3), .B_i(B_3), .C_i(n1_bit_adder_5_c_i_1), .S_i(S_i_3), .C_i_1(n1_bit_adder_4_c_i_1));
  _1_bit_adder u_1_bit_adder_5 (
    .A_i(A_4), .B_i(B_4), .C_i(n1_bit_adder_6_c_i_1), .S_i(S_i_4), .C_i_1(n1_bit_adder_5_c_i_1));
  _1_bit_adder u_1_bit_adder_6 (
    .A_i(A_5), .B_i(B_5), .C_i(n1_bit_adder_7_c_i_1), .S_i(S_i_5), .C_i_1(n1_bit_adder_6_c_i_1));
  _1_bit_adder u_1_bit_adder_7 (
    .A_i(A_6), .B_i(B_6), .C_i(n1_bit_adder_8_c_i_1), .S_i(S_i_6), .C_i_1(n1_bit_adder_7_c_i_1));
  _1_bit_adder u_1_bit_adder_8 (
    .A_i(A_7), .B_i(B_7), .C_i(n1_bit_adder_9_c_i_1), .S_i(S_i_7), .C_i_1(n1_bit_adder_8_c_i_1));
  _1_bit_adder u_1_bit_adder_9 (
    .A_i(A_8), .B_i(B_8), .C_i(n1_bit_adder_10_c_i_1), .S_i(S_i_8), .C_i_1(n1_bit_adder_9_c_i_1));
  _1_bit_adder u_1_bit_adder_10 (
    .A_i(A_9), .B_i(B_9), .C_i(n1_bit_adder_11_c_i_1), .S_i(S_i_9), .C_i_1(n1_bit_adder_10_c_i_1));
  _1_bit_adder u_1_bit_adder_11 (
    .A_i(A_10), .B_i(B_10), .C_i(n1_bit_adder_12_c_i_1), .S_i(S_i_10), .C_i_1(n1_bit_adder_11_c_i_1));
  _1_bit_adder u_1_bit_adder_12 (
    .A_i(A_11), .B_i(B_11), .C_i(n1_bit_adder_13_c_i_1), .S_i(S_i_11), .C_i_1(n1_bit_adder_12_c_i_1));
  _1_bit_adder u_1_bit_adder_13 (
    .A_i(A_12), .B_i(B_12), .C_i(n1_bit_adder_14_c_i_1), .S_i(S_i_12), .C_i_1(n1_bit_adder_13_c_i_1));
  _1_bit_adder u_1_bit_adder_14 (
    .A_i(A_13), .B_i(B_13), .C_i(n1_bit_adder_15_c_i_1), .S_i(S_i_13), .C_i_1(n1_bit_adder_14_c_i_1));
  _1_bit_adder u_1_bit_adder_15 (
    .A_i(A_14), .B_i(B_14), .C_i(n1_bit_adder_16_c_i_1), .S_i(S_i_14), .C_i_1(n1_bit_adder_15_c_i_1));
  _1_bit_adder u_1_bit_adder_16 (
    .A_i(A_15), .B_i(B_15), .C_i(n1_bit_adder_17_c_i_1), .S_i(S_i_15), .C_i_1(n1_bit_adder_16_c_i_1));
  _1_bit_adder u_1_bit_adder_17 (
    .A_i(A_16), .B_i(B_16), .C_i(n1_bit_adder_18_c_i_1), .S_i(S_i_16), .C_i_1(n1_bit_adder_17_c_i_1));
  _1_bit_adder u_1_bit_adder_18 (
    .A_i(A_17), .B_i(B_17), .C_i(n1_bit_adder_19_c_i_1), .S_i(S_i_17), .C_i_1(n1_bit_adder_18_c_i_1));
  _1_bit_adder u_1_bit_adder_19 (
    .A_i(A_18), .B_i(B_18), .C_i(n1_bit_adder_20_c_i_1), .S_i(S_i_18), .C_i_1(n1_bit_adder_19_c_i_1));
  _1_bit_adder u_1_bit_adder_20 (
    .A_i(A_19), .B_i(B_19), .C_i(n1_bit_adder_21_c_i_1), .S_i(S_i_19), .C_i_1(n1_bit_adder_20_c_i_1));
  _1_bit_adder u_1_bit_adder_21 (
    .A_i(A_20), .B_i(B_20), .C_i(n1_bit_adder_22_c_i_1), .S_i(S_i_20), .C_i_1(n1_bit_adder_21_c_i_1));
  _1_bit_adder u_1_bit_adder_22 (
    .A_i(A_21), .B_i(B_21), .C_i(n1_bit_adder_23_c_i_1), .S_i(S_i_21), .C_i_1(n1_bit_adder_22_c_i_1));
  _1_bit_adder u_1_bit_adder_23 (
    .A_i(A_22), .B_i(B_22), .C_i(n1_bit_adder_24_c_i_1), .S_i(S_i_22), .C_i_1(n1_bit_adder_23_c_i_1));
  _1_bit_adder u_1_bit_adder_24 (
    .A_i(A_23), .B_i(B_23), .C_i(n1_bit_adder_25_c_i_1), .S_i(S_i_23), .C_i_1(n1_bit_adder_24_c_i_1));
  _1_bit_adder u_1_bit_adder_25 (
    .A_i(A_24), .B_i(B_24), .C_i(n1_bit_adder_26_c_i_1), .S_i(S_i_24), .C_i_1(n1_bit_adder_25_c_i_1));
  _1_bit_adder u_1_bit_adder_26 (
    .A_i(A_25), .B_i(B_25), .C_i(n1_bit_adder_27_c_i_1), .S_i(S_i_25), .C_i_1(n1_bit_adder_26_c_i_1));
  _1_bit_adder u_1_bit_adder_27 (
    .A_i(A_26), .B_i(B_26), .C_i(n1_bit_adder_28_c_i_1), .S_i(S_i_26), .C_i_1(n1_bit_adder_27_c_i_1));
  _1_bit_adder u_1_bit_adder_28 (
    .A_i(A_27), .B_i(B_27), .C_i(n1_bit_adder_29_c_i_1), .S_i(S_i_27), .C_i_1(n1_bit_adder_28_c_i_1));
  _1_bit_adder u_1_bit_adder_29 (
    .A_i(A_28), .B_i(B_28), .C_i(n1_bit_adder_30_c_i_1), .S_i(S_i_28), .C_i_1(n1_bit_adder_29_c_i_1));
  _1_bit_adder u_1_bit_adder_30 (
    .A_i(A_29), .B_i(B_29), .C_i(n1_bit_adder_31_c_i_1), .S_i(S_i_29), .C_i_1(n1_bit_adder_30_c_i_1));
  _1_bit_adder u_1_bit_adder_31 (
    .A_i(A_30), .B_i(B_30), .C_i(n1_bit_adder_32_c_i_1), .S_i(S_i_30), .C_i_1(n1_bit_adder_31_c_i_1));
  _1_bit_adder u_1_bit_adder_32 (.A_i(A_31), .B_i(B_31), .C_i(c_i), .S_i(S_i_31), .C_i_1(n1_bit_adder_32_c_i_1));
endmodule

module _32_bit_adder (
  input  [31:0] A,
  input  C_i,
  input  [31:0] B,
  output C_i_1,
  output [31:0] R
);

  _32_bit_adder_helper u_32_bit_adder_helper_1 (
    .c_i(C_i), .A_MSB(A[31]), .A(A[30]), .A_2(A[29]), .A_3(A[28]), .A_4(A[27]), .A_5(A[26]), .A_6(A[25]),
    .A_7(A[24]), .A_8(A[23]), .A_9(A[22]), .A_10(A[21]), .A_11(A[20]), .A_12(A[19]), .A_13(A[18]),
    .A_14(A[17]), .A_15(A[16]), .A_16(A[15]), .A_17(A[14]), .A_18(A[13]), .A_19(A[12]), .A_20(A[11]),
    .A_21(A[10]), .A_22(A[9]), .A_23(A[8]), .A_24(A[7]), .A_25(A[6]), .A_26(A[5]), .A_27(A[4]), .A_28(A[3]),
    .A_29(A[2]), .A_30(A[1]), .A_31(A[0]), .B_MSB(B[31]), .B(B[30]), .B_2(B[29]), .B_3(B[28]), .B_4(B[27]),
    .B_5(B[26]), .B_6(B[25]), .B_7(B[24]), .B_8(B[23]), .B_9(B[22]), .B_10(B[21]), .B_11(B[20]),
    .B_12(B[19]), .B_13(B[18]), .B_14(B[17]), .B_15(B[16]), .B_16(B[15]), .B_17(B[14]), .B_18(B[13]),
    .B_19(B[12]), .B_20(B[11]), .B_21(B[10]), .B_22(B[9]), .B_23(B[8]), .B_24(B[7]), .B_25(B[6]),
    .B_26(B[5]), .B_27(B[4]), .B_28(B[3]), .B_29(B[2]), .B_30(B[1]), .B_31(B[0]), .C_i_1(C_i_1),
    .S_i_MSB(R[31]), .S_i(R[30]), .S_i_2(R[29]), .S_i_3(R[28]), .S_i_4(R[27]), .S_i_5(R[26]), .S_i_6(R[25]),
    .S_i_7(R[24]), .S_i_8(R[23]), .S_i_9(R[22]), .S_i_10(R[21]), .S_i_11(R[20]), .S_i_12(R[19]),
    .S_i_13(R[18]), .S_i_14(R[17]), .S_i_15(R[16]), .S_i_16(R[15]), .S_i_17(R[14]), .S_i_18(R[13]),
    .S_i_19(R[12]), .S_i_20(R[11]), .S_i_21(R[10]), .S_i_22(R[9]), .S_i_23(R[8]), .S_i_24(R[7]),
    .S_i_25(R[6]), .S_i_26(R[5]), .S_i_27(R[4]), .S_i_28(R[3]), .S_i_29(R[2]), .S_i_30(R[1]), .S_i_31(R[0]));
endmodule
