// Logisim project mult32.circ as structural Verilog: 3 circuits, main circuit main
module main (
  input  [31:0] Multiplicand,
  input  [31:0] Multiplier,
  output [31:0] Most_Significant_Bits,
  output [31:0] Least_Significant_Bits
);

  wire clock_1_out, main_1_count, main_1_enable, main_1_init, main_1_overflow_clr, main_1_overflow_en,
       main_1_shift, main_2_is_done, main_2_product0_isone, Start_out;

  Button Start (.out(Start_out));
  control_main main_1 (
    .start(Start_out), .product0(main_2_product0_isone), .done(main_2_is_done), .enable_state_register(1'b1),
    .clear_state_register(1'b0), .CLK(clock_1_out), .overflow_en(main_1_overflow_en),
    .overflow_clr(main_1_overflow_clr), .init(main_1_init), .shift(main_1_shift), .enable(main_1_enable),
    .count(main_1_count));
  datapath_main main_2 (
    .overflow_en(main_1_overflow_en), .overflow_clr(main_1_overflow_clr), .init(main_1_init),
    .shift(main_1_shift), .enable(main_1_enable), .CLK(clock_1_out), .clear(1'b0), .count(main_1_count),
    .Multiplicand(Multiplicand), .Multiplier(Multiplier), .Mostignificant(Most_Significant_Bits),
    .LeastSignificant(Least_Significant_Bits), .product0_isOne(main_2_product0_isone),
    .is_done(main_2_is_done));  // open: isOverFlow
  Clock clock_1 (.out(clock_1_out));
endmodule

module Tests (
  output [31:0] out_1,
  output [31:0] out_2,
  output [31:0] out_3,
  output [31:0] out_4,
  output [31:0] out_5,
  output [31:0] out_6,
  output [31:0] out_7,
  output [31:0] out_8,
  output [31:0] out_9,
  output [31:0] out_10,
  output [31:0] out_11,
  output [31:0] out_12,
  output [31:0] out_13,
  output [31:0] out_14,
  output [31:0] out_15,
  output [31:0] out_16,
  output [31:0] out_17,
  output [31:0] out_18,
  output [31:0] out_19,
  output [31:0] out_20,
  output [31:0] out_21,
  output [31:0] out_22,
  output [31:0] out_23,
  output [31:0] out_24,
  output [31:0] out_25,
  output [31:0] out_26,
  output [31:0] out_27,
  output [31:0] out_28,
  output [31:0] out_29,
  output [31:0] out_30
);

  wire clock_1_out, Start_Tests_out;

  Button Start_Tests (.out(Start_Tests_out));
  Test_Helper test_helper_1 (
    .Start(Start_Tests_out), .Multiplicand({32{1'b0}}), .Multiplier(32'hffff), .Most_Significant_Bits(out_1),
    .Least_Significant_Bits(out_2), .CLK(clock_1_out));
  Test_Helper test_helper_2 (
    .Start(Start_Tests_out), .Multiplicand(32'hff), .Multiplier(32'hffff), .Most_Significant_Bits(out_9),
    .Least_Significant_Bits(out_10), .CLK(clock_1_out));
  Test_Helper test_helper_3 (
    .Start(Start_Tests_out), .Multiplicand(32'h55555555), .Multiplier(32'haaaaaaaa),
    .Most_Significant_Bits(out_17), .Least_Significant_Bits(out_18), .CLK(clock_1_out));
  Test_Helper test_helper_4 (
    .Start(Start_Tests_out), .Multiplicand(32'h24), .Multiplier(32'h11), .Most_Significant_Bits(out_25),
    .Least_Significant_Bits(out_26), .CLK(clock_1_out));
  Test_Helper test_helper_5 (
    .Start(Start_Tests_out), .Multiplicand(32'hffff00), .Multiplier({32{1'b0}}),
    .Most_Significant_Bits(out_3), .Least_Significant_Bits(out_4), .CLK(clock_1_out));
  Test_Helper test_helper_6 (
    .Start(Start_Tests_out), .Multiplicand(32'hffff), .Multiplier(32'hff), .Most_Significant_Bits(out_11),
    .Least_Significant_Bits(out_12), .CLK(clock_1_out));
  Test_Helper test_helper_7 (
    .Start(Start_Tests_out), .Multiplicand(32'haaaaaaaa), .Multiplier(32'h55555555),
    .Most_Significant_Bits(out_19), .Least_Significant_Bits(out_20), .CLK(clock_1_out));
  Test_Helper test_helper_8 (
    .Start(Start_Tests_out), .Multiplicand(32'h11), .Multiplier(32'h24), .Most_Significant_Bits(out_27),
    .Least_Significant_Bits(out_28), .CLK(clock_1_out));
  Test_Helper test_helper_9 (
    .Start(Start_Tests_out), .Multiplicand(32'hff), .Multiplier(32'h1), .Most_Significant_Bits(out_5),
    .Least_Significant_Bits(out_6), .CLK(clock_1_out));
  Test_Helper test_helper_10 (
    .Start(Start_Tests_out), .Multiplicand(32'h55aa), .Multiplier(32'h55), .Most_Significant_Bits(out_13),
    .Least_Significant_Bits(out_14), .CLK(clock_1_out));
  Test_Helper test_helper_11 (
    .Start(Start_Tests_out), .Multiplicand(32'h18244281), .Multiplier(32'h81422418),
    .Most_Significant_Bits(out_21), .Least_Significant_Bits(out_22), .CLK(clock_1_out));
  Test_Helper test_helper_12 (
    .Start(Start_Tests_out), .Multiplicand({32{1'b1}}), .Multiplier({32{1'b1}}),
    .Most_Significant_Bits(out_29), .Least_Significant_Bits(out_30), .CLK(clock_1_out));
  Test_Helper test_helper_13 (
    .Start(Start_Tests_out), .Multiplicand(32'h1), .Multiplier(32'hffff), .Most_Significant_Bits(out_7),
    .Least_Significant_Bits(out_8), .CLK(clock_1_out));
  Test_Helper test_helper_14 (
    .Start(Start_Tests_out), .Multiplicand(32'h55), .Multiplier(32'h55aa), .Most_Significant_Bits(out_15),
    .Least_Significant_Bits(out_16), .CLK(clock_1_out));
  Test_Helper test_helper_15 (
    .Start(Start_Tests_out), .Multiplicand(32'h81422418), .Multiplier(32'h18244281),
    .Most_Significant_Bits(out_23), .Least_Significant_Bits(out_24), .CLK(clock_1_out));
  Clock clock_1 (.out(clock_1_out));

  // Notes on the sheet:
  //   Test Case 1
  //   Test Case 3
  //   Test Case 5
  //   Test Case 7
  //   Test Case 8
  //   Test Case 2
  //   Test Case 4
  //   Test Case 6
endmodule

module Test_Helper (
  input  Start,
  input  [31:0] Multiplicand,
  input  [31:0] Multiplier,
  input  CLK,
  output [31:0] Most_Significant_Bits,
  output [31:0] Least_Significant_Bits
);

  wire main_1_count, main_1_enable, main_1_init, main_1_overflow_clr, main_1_overflow_en, main_1_shift,
       main_2_is_done, main_2_product0_isone;

  control_main main_1 (
    .start(Start), .product0(main_2_product0_isone), .done(main_2_is_done), .enable_state_register(1'b1),
    .clear_state_register(1'b0), .CLK(CLK), .overflow_en(main_1_overflow_en),
    .overflow_clr(main_1_overflow_clr), .init(main_1_init), .shift(main_1_shift), .enable(main_1_enable),
    .count(main_1_count));
  datapath_main main_2 (
    .overflow_en(main_1_overflow_en), .overflow_clr(main_1_overflow_clr), .init(main_1_init),
    .shift(main_1_shift), .enable(main_1_enable), .CLK(CLK), .clear(1'b0), .count(main_1_count),
    .Multiplicand(Multiplicand), .Multiplier(Multiplier), .Mostignificant(Most_Significant_Bits),
    .LeastSignificant(Least_Significant_Bits), .product0_isOne(main_2_product0_isone),
    .is_done(main_2_is_done));  // open: isOverFlow
endmodule
